// Logisim project ALU.circ as structural Verilog: 2 circuits, main circuit main
module main (
  input  a4,
  input  a3,
  input  b4,
  input  b3,
  input  a5,
  input  a2,
  input  b5,
  input  b2,
  input  a6,
  input  a1,
  input  b6,
  input  b1,
  input  a7,
  input  a0,
  input  b7,
  input  b0,
  input  s0,
  input  s1,
  input  s2,
  output b4_2,
  output b3_2,
  output b5_2,
  output b2_2,
  output overflow,
  output b6_2,
  output b1_2,
  output b7_2,
  output b0_2
);

  wire and_1_out, C1, C2, decoder_1_out2, decoder_1_out3, decoder_1_out4, isneg_1_out_2, isneg_2_out_2, OF01,
       OF2, xor_1_out;
  wire [7:0] demultiplexer_1_out0, demultiplexer_1_out1, demultiplexer_2_out0, demultiplexer_2_out1,
       demultiplexer_3_out0, demultiplexer_3_out1, demultiplexer_4_out0, demultiplexer_4_out1, or_1_out,
       or_2_out, or_3_out, R01, R2, R3, R4, R5, R6, R7, RTMP, signchange_1_out, signchange_2_out,
       signchange_3_out, signchange_4_out;

  Demultiplexer #(.width(8), .enable("false")) demultiplexer_1 (
    .out0(demultiplexer_1_out0), .out1(demultiplexer_1_out1), .in({b7, b6, b5, b4, b3, b2, b1, b0}), .sel(C1));
  Demultiplexer #(.width(8), .enable("false")) demultiplexer_2 (
    .out0(demultiplexer_2_out0), .out1(demultiplexer_2_out1), .in({a7, a6, a5, a4, a3, a2, a1, a0}),
    .sel(isneg_1_out_2));
  Demultiplexer #(.width(8), .enable("false")) demultiplexer_3 (
    .out0(demultiplexer_3_out0), .out1(demultiplexer_3_out1), .in({b7, b6, b5, b4, b3, b2, b1, b0}),
    .sel(isneg_2_out_2));
  assign or_1_out = demultiplexer_1_out0 | signchange_1_out;  // OR_Gate or_1, 8 bits wide
  SignChange signchange_1 (.Num(demultiplexer_1_out1), .out(signchange_1_out));
  SignChange signchange_2 (.Num(demultiplexer_2_out1), .out(signchange_2_out));
  IsNeg isneg_1 (.A({a7, a6, a5, a4, a3, a2, a1, a0}), .out_2(isneg_1_out_2));
  SignChange signchange_3 (.Num(demultiplexer_3_out1), .out(signchange_3_out));
  IsNeg isneg_2 (.A({b7, b6, b5, b4, b3, b2, b1, b0}), .out_2(isneg_2_out_2));
  Soma8bits soma8bits_1 (.Num1(or_1_out), .Num2({a7, a6, a5, a4, a3, a2, a1, a0}), .Result(R01), .Overflow(OF01));
  assign or_2_out = demultiplexer_2_out0 | signchange_2_out;  // OR_Gate or_2, 8 bits wide
  assign or_3_out = demultiplexer_3_out0 | signchange_3_out;  // OR_Gate or_3, 8 bits wide
  MultLib_main main_1 (.In(or_3_out), .In_2(or_2_out), .Overflow(OF2), .out_4(R2));
  QucienteResto qucienteresto_1 (.B(or_3_out), .A(or_2_out), .A_B(R3), .A_B_2(R4));
  xor xor_1 (xor_1_out, isneg_1_out_2, isneg_2_out_2);
  and and_1 (and_1_out, xor_1_out, C2);
  Demultiplexer #(.width(8), .enable("false")) demultiplexer_4 (
    .out0(demultiplexer_4_out0), .out1(demultiplexer_4_out1), .in(RTMP), .sel(and_1_out));
  Decoder #(.select(3), .enable("false")) decoder_1 (
    .out1(C1), .out2(decoder_1_out2), .out3(decoder_1_out3), .out4(decoder_1_out4), .sel({s2, s1, s0}));  // open: out0, out5, out6, out7
  or or_4 (C2, decoder_1_out2, decoder_1_out3, decoder_1_out4);
  SignChange signchange_4 (.Num(demultiplexer_4_out1), .out(signchange_4_out));
  Multiplexer #(.select(3), .width(8), .enable("false")) multiplexer_1 (
    .in0(R01), .in1(R01), .in2(R2), .in3(R3), .in4(R4), .in5(R5), .in6(R6), .in7(R7), .out(RTMP),
    .sel({s2, s1, s0}));
  assign {b7_2, b6_2, b5_2, b4_2, b3_2, b2_2, b1_2, b0_2} = demultiplexer_4_out0 | signchange_4_out;  // OR_Gate or_5, 8 bits wide
  Multiplexer #(.select(3), .enable("false")) multiplexer_2 (
    .in0(OF01), .in1(OF01), .in2(OF2), .in3(1'b0), .in4(1'b0), .in5(1'b0), .in6(1'b0), .in7(1'b0),
    .out(overflow), .sel({s2, s1, s0}));
  Shifter shifter_1 (.in({a7, a6, a5, a4, a3, a2, a1, a0}), .\dist ({b2, b1, b0}), .out(R5));
  Shifter #(.shift("lr")) shifter_2 (.in({a7, a6, a5, a4, a3, a2, a1, a0}), .\dist ({b2, b1, b0}), .out(R6));
  SignChange signchange_5 (.Num({a7, a6, a5, a4, a3, a2, a1, a0}), .out(R7));

  // Other names for the same wires on the sheet: of = overflow;
  //   R[7:0] = {b7_2, b6_2, b5_2, b4_2, b3_2, b2_2, b1_2, b0_2}

  // Notes on the sheet:
  //   SOMA E SUBTRAÇÃO
  //   MULTIPLIÇÃO E DIVISÃO
  //   INVERSOR DE SINAL
  //   SELETOR DE SAÍDA
endmodule

module IsNeg (
  input  [7:0] A,
  output out_2
);


  assign out_2 = A[7];
endmodule
