// Logisim project FDX.circ as structural Verilog: 4 circuits, main circuit main
module main (
);

  wire and_14_out, and_15_out, and_16_out, Clock, clock_1_out, comparator_1_eq, comparator_1_gt,
       comparator_1_lt, d_ff_1_qn, Input, isequal8_1_out_3, isequal8_2_out_3, isequal8_3_out_3,
       isequal8_4_out_3, isequal8_5_out_3, isequal8_6_out_3, isequal8_7_out_3, isequal8_8_out_3,
       isequal8_9_out_3, isequal8_10_out_3, isequal8_11_out_3, isequal8_12_out_3, isequal8_13_out_3,
       isequal8_14_out_3, isequal8_15_out_3, isequal8_16_out_3, isequal8_17_out_3, keyboard_1_avail, KILL,
       nor_1_out, not_1_out, not_2_out, not_3_out, not_4_out, not_5_out, not_6_out, not_7_out, or_1_out,
       or_2_out, or_3_out, or_4_out, or_5_out, or_6_out, or_7_out, or_8_out, or_9_out, or_10_out, or_11_out,
       or_12_out, or_13_out, or_14_out, or_15_out, or_16_out, or_17_out, or_18_out, or_19_out, or_20_out,
       or_21_out, or_22_out, or_23_out, or_24_out, or_25_out, or_26_out, or_27_out, or_28_out, or_29_out,
       or_30_out, or_32_out, or_33_out, or_34_out, or_35_out, or_38_out, or_39_out, or_40_out, or_41_out,
       or_42_out, or_43_out, or_44_out, or_45_out, or_46_out, or_47_out, or_48_out, or_49_out, Output,
       Over_Zero, pull_resistor_1_node, pull_resistor_2_node, pull_resistor_3_node, pull_resistor_4_node,
       pull_resistor_5_node, pull_resistor_6_node, pull_resistor_7_node, pull_resistor_8_node,
       pull_resistor_9_node, pull_resistor_10_node, pull_resistor_11_node, pull_resistor_12_node,
       pull_resistor_13_node, pull_resistor_14_node, pull_resistor_15_node, ReadWrite, SelectMen, ToAcu,
       tunnel, tunnel_t, tunnel_t_t, WriteAcu, WriteIR, WritePC, WritePC2;
  wire [2:0] AluControl;
  wire [6:0] keyboard_1_data;
  wire [7:0] Controle, controlled_buffer_1_out, IR_q, multiplexer_1_out, PC_q;
  wire [15:0] ACC, alu_1_saida, controlled_buffer_4_out, demultiplexer_1_out1, MEMORIA, multiplexer_2_out,
       multiplexer_3_out, OutputData, ram_1_data;

  Clock clock_1 (.out(clock_1_out));
  not not_1 (not_1_out, or_1_out);
  or or_1 (or_1_out, KILL, Over_Zero);
  and and_1 (Clock, clock_1_out, not_1_out);
  assign controlled_buffer_1_out = WritePC2 ? IR_q : 8'bz;  // Controlled_Buffer controlled_buffer_1
  not not_2 (not_2_out, or_24_out);
  IsEqual8 isequal8_1 (.in_1(Controle), .in_2(8'hb), .out_3(isequal8_1_out_3));
  IsEqual8 isequal8_2 (.in_1(Controle), .in_2(8'hc), .out_3(isequal8_2_out_3));
  IsEqual8 isequal8_3 (.in_1(Controle), .in_2(8'h1b), .out_3(isequal8_3_out_3));
  IsEqual8 isequal8_4 (.in_1(Controle), .in_2(8'h46), .out_3(isequal8_4_out_3));
  IsEqual8 isequal8_5 (.in_1(Controle), .in_2(8'h15), .out_3(isequal8_5_out_3));
  IsEqual8 isequal8_6 (.in_1(Controle), .in_2(8'h16), .out_3(isequal8_6_out_3));
  IsEqual8 isequal8_7 (.in_1(Controle), .in_2(8'h17), .out_3(isequal8_7_out_3));
  IsEqual8 isequal8_8 (.in_1(Controle), .in_2(8'h18), .out_3(isequal8_8_out_3));
  IsEqual8 isequal8_9 (.in_1(Controle), .in_2(8'h19), .out_3(isequal8_9_out_3));
  IsEqual8 isequal8_10 (.in_1(Controle), .in_2(8'h34), .out_3(isequal8_10_out_3));
  IsEqual8 isequal8_11 (.in_1(Controle), .in_2(8'h35), .out_3(isequal8_11_out_3));
  IsEqual8 isequal8_12 (.in_1(Controle), .in_2(8'h36), .out_3(isequal8_12_out_3));
  IsEqual8 isequal8_13 (.in_1(Controle), .in_2(8'h37), .out_3(isequal8_13_out_3));
  IsEqual8 isequal8_14 (.in_1(Controle), .in_2(8'h38), .out_3(isequal8_14_out_3));
  IsEqual8 isequal8_15 (.in_1(Controle), .in_2(8'h39), .out_3(isequal8_15_out_3));
  IsEqual8 isequal8_16 (.in_1(Controle), .in_2(8'h1f), .out_3(isequal8_16_out_3));
  IsEqual8 isequal8_17 (.in_1(Controle), .in_2(8'h29), .out_3(isequal8_17_out_3));
  or or_2 (or_2_out, not_2_out, d_ff_1_qn);
  Counter PC (
    .load(WritePC2), .D(controlled_buffer_1_out), .count(nor_1_out), .Q(PC_q), .clk(Clock));  // open: carry, clr
  nor nor_1 (nor_1_out, WritePC2, SelectMen);
  not not_3 (not_3_out, WriteIR);
  or or_3 (or_3_out, isequal8_1_out_3, pull_resistor_1_node);
  or or_4 (or_4_out, isequal8_5_out_3, or_3_out);
  or or_5 (or_5_out, isequal8_6_out_3, or_4_out);
  or or_6 (or_6_out, isequal8_7_out_3, or_5_out);
  or or_7 (or_7_out, isequal8_8_out_3, or_6_out);
  or or_8 (or_8_out, isequal8_9_out_3, or_7_out);
  and and_2 (WriteAcu, not_4_out, or_8_out);
  not not_4 (not_4_out, d_ff_1_qn);
  D_Flip_Flop d_ff_1 (.clk(Clock), .D(or_2_out), .Qn(d_ff_1_qn));  // open: Q, preset, en, reset
  Register #(.width(16)) IR (.D(MEMORIA), .en(not_3_out), .Q({Controle, IR_q}), .clk(Clock));  // open: clr
  Pull_Resistor pull_resistor_1 (.node(pull_resistor_1_node));
  Pull_Resistor pull_resistor_2 (.node(pull_resistor_2_node));
  or or_9 (or_9_out, isequal8_1_out_3, pull_resistor_2_node);
  or or_10 (or_10_out, isequal8_2_out_3, or_9_out);
  or or_11 (or_11_out, isequal8_3_out_3, or_10_out);
  or or_12 (or_12_out, isequal8_5_out_3, or_11_out);
  or or_13 (or_13_out, isequal8_6_out_3, or_12_out);
  or or_14 (or_14_out, isequal8_7_out_3, or_13_out);
  or or_15 (or_15_out, isequal8_8_out_3, or_14_out);
  or or_16 (or_16_out, isequal8_9_out_3, or_15_out);
  or or_17 (or_17_out, isequal8_10_out_3, or_16_out);
  or or_18 (or_18_out, isequal8_11_out_3, or_17_out);
  or or_19 (or_19_out, isequal8_12_out_3, or_18_out);
  or or_20 (or_20_out, isequal8_13_out_3, or_19_out);
  or or_21 (or_21_out, isequal8_14_out_3, or_20_out);
  or or_22 (or_22_out, isequal8_15_out_3, or_21_out);
  or or_23 (or_23_out, isequal8_16_out_3, or_22_out);
  or or_24 (or_24_out, isequal8_17_out_3, or_23_out);
  and and_3 (SelectMen, not_4_out, or_24_out);
  Multiplexer #(.width(8), .enable("false")) multiplexer_1 (
    .in0(PC_q), .in1(IR_q), .out(multiplexer_1_out), .sel(SelectMen));
  Pull_Resistor pull_resistor_3 (.node(pull_resistor_3_node));
  Pull_Resistor pull_resistor_4 (.node(pull_resistor_4_node));
  or or_25 (or_25_out, isequal8_2_out_3, pull_resistor_4_node);
  or or_26 (or_26_out, isequal8_3_out_3, pull_resistor_3_node);
  or or_27 (or_27_out, isequal8_16_out_3, or_25_out);
  and and_4 (WritePC, not_4_out, or_26_out);
  and and_5 (ReadWrite, not_4_out, or_27_out);
  Pull_Resistor pull_resistor_5 (.node(pull_resistor_5_node));
  and and_6 (WriteIR, not_4_out, pull_resistor_5_node);
  RAM #(.dataWidth(16)) ram_1 (
    .addr(multiplexer_1_out), .data(ram_1_data), .clk(Clock), .ld(not_5_out));  // open: sel, clr
  not not_5 (not_5_out, ReadWrite);
  Pull_Resistor pull_resistor_6 (.node(pull_resistor_6_node));
  Pull_Resistor pull_resistor_7 (.node(pull_resistor_7_node));
  or or_28 (or_28_out, isequal8_1_out_3, pull_resistor_6_node);
  or or_29 (or_29_out, isequal8_5_out_3, pull_resistor_7_node);
  or or_30 (or_30_out, isequal8_6_out_3, or_29_out);
  or or_31 (AluControl[2], isequal8_7_out_3, or_30_out);
  and and_7 (ToAcu, not_4_out, or_28_out);
  assign OutputData = not_6_out ? ram_1_data : 16'bz;  // Controlled_Buffer controlled_buffer_2
  not not_6 (not_6_out, ReadWrite);
  assign ram_1_data = ReadWrite ? multiplexer_2_out : 16'bz;  // Controlled_Buffer controlled_buffer_3
  Pull_Resistor pull_resistor_8 (.node(pull_resistor_8_node));
  or or_32 (or_32_out, isequal8_5_out_3, pull_resistor_10_node);
  or or_33 (or_33_out, isequal8_6_out_3, pull_resistor_8_node);
  or or_34 (or_34_out, isequal8_7_out_3, or_33_out);
  or or_35 (or_35_out, isequal8_7_out_3, or_32_out);
  or or_36 (AluControl[1], isequal8_8_out_3, or_34_out);
  or or_37 (AluControl[0], isequal8_9_out_3, or_35_out);
  Demultiplexer #(.width(16), .enable("false")) demultiplexer_1 (
    .out0(MEMORIA), .out1(demultiplexer_1_out1), .in(OutputData), .sel(ToAcu));
  Pull_Resistor pull_resistor_9 (.node(pull_resistor_9_node));
  Pull_Resistor pull_resistor_10 (.node(pull_resistor_10_node));
  or or_38 (or_38_out, isequal8_10_out_3, pull_resistor_9_node);
  or or_39 (or_39_out, isequal8_11_out_3, or_38_out);
  or or_40 (or_40_out, isequal8_14_out_3, or_39_out);
  and and_8 (tunnel, not_4_out, or_40_out);
  assign controlled_buffer_4_out = ToAcu ? demultiplexer_1_out1 : 16'bz;  // Controlled_Buffer controlled_buffer_4
  Multiplexer #(.width(16), .enable("false")) multiplexer_2 (
    .in0(ACC), .in1(multiplexer_3_out), .out(multiplexer_2_out), .sel(Input));
  Pull_Resistor pull_resistor_11 (.node(pull_resistor_11_node));
  Pull_Resistor pull_resistor_12 (.node(pull_resistor_12_node));
  or or_41 (or_41_out, isequal8_10_out_3, pull_resistor_11_node);
  or or_42 (or_42_out, isequal8_11_out_3, pull_resistor_12_node);
  or or_43 (or_43_out, isequal8_12_out_3, or_42_out);
  or or_44 (or_44_out, isequal8_13_out_3, or_41_out);
  or or_45 (or_45_out, isequal8_15_out_3, or_43_out);
  or or_46 (or_46_out, isequal8_15_out_3, or_44_out);
  and and_9 (tunnel_t_t, not_4_out, or_45_out);
  and and_10 (tunnel_t, not_4_out, or_46_out);
  not not_7 (not_7_out, ToAcu);
  assign controlled_buffer_4_out = not_7_out ? alu_1_saida : 16'bz;  // Controlled_Buffer controlled_buffer_5
  Keyboard keyboard_1 (.clk(Clock), .re(Input), .avail(keyboard_1_avail), .data(keyboard_1_data));  // open: clr
  Pull_Resistor pull_resistor_13 (.node(pull_resistor_13_node));
  or or_47 (or_47_out, isequal8_4_out_3, pull_resistor_13_node);
  and and_11 (KILL, not_4_out, or_47_out);
  Register #(.width(16)) Acu (.D(controlled_buffer_4_out), .en(WriteAcu), .Q(ACC), .clk(Clock));  // open: clr
  Pull_Resistor pull_resistor_14 (.node(pull_resistor_14_node));
  Pull_Resistor pull_resistor_15 (.node(pull_resistor_15_node));
  or or_48 (or_48_out, isequal8_16_out_3, pull_resistor_14_node);
  or or_49 (or_49_out, isequal8_17_out_3, pull_resistor_15_node);
  and and_12 (Input, not_4_out, or_48_out);
  and and_13 (Output, not_4_out, or_49_out);
  ALU alu_1 (.A(ACC), .B(MEMORIA), .SELECT(AluControl), .OVERFLOW(Over_Zero), .SAIDA(alu_1_saida));
  Multiplexer #(.width(16), .enable("false")) multiplexer_3 (
    .in0({16{1'b1}}), .in1({{9{1'b0}}, keyboard_1_data}), .out(multiplexer_3_out), .sel(keyboard_1_avail));
  Comparator #(.width(16)) comparator_1 (
    .a(ACC), .b({16{1'b0}}), .gt(comparator_1_gt), .eq(comparator_1_eq), .lt(comparator_1_lt));
  TTY tty_1 (.data(OutputData[6:0]), .clk(Clock), .we(Output));  // open: clr
  and and_14 (and_14_out, comparator_1_gt, tunnel_t_t);
  and and_15 (and_15_out, comparator_1_eq, tunnel_t);
  and and_16 (and_16_out, comparator_1_lt, tunnel);
  or or_50 (WritePC2, and_14_out, and_15_out, and_16_out, WritePC);

  // Notes on the sheet:
  //   Desvia para  XY se ACC  menor ou igual a zero
  //   Carrega dado do endereço AB no acumulador
  //   Carrega acumulador no endereço AB
  //   Salto não condicional para AB
  //   Fim de execução
  //   Soma ACC com conteúdo do endereço XY
  //   Subtrai conteúdo do endereço XY de ACC
  //   Multiplica ACC pelo conteudo do endereco XY
  //   Divide ACC pelo conteudo do endereco XY
  //   Resto da divis˜ao de ACC pelo conteudo do endereco XY
  //   Idem, diferente de zero
  //   Idem, maior que zero
  //   Idem, igual a zero
  //   Idem, menor que zero
  //   Idem, maior ou igual a zero
  //   Le entrada e armazena em XY
  //    Escreve na saıda o conteudo da posicao XY
  //   Se fizer referencia a endereço de memoria
endmodule

module IsEqual8 (
  input  [7:0] in_1,
  input  [7:0] in_2,
  output out_3
);

  Comparator comparator_1 (.a(in_1), .b(in_2), .eq(out_3));  // open: gt, lt
endmodule

module ALU (
  input  [15:0] A,
  input  [15:0] B,
  input  [2:0] SELECT,
  output OVERFLOW,
  output [15:0] SAIDA
);

  wire and_1_out, comparator_1_lt, comparator_2_lt, DIVOVER, MULTOVER, SOMAOVER, SUBOVER;
  wire [15:0] DIV, divider_1_out, divider_1_rem, MULT, multiplexer_2_out, multiplexer_3_out,
       multiplier_1_cout, multiplier_1_out, negator_1_out, negator_2_out, negator_3_out, negator_4_out,
       negator_5_out, REST, SOMA, SUB;

  Negator #(.width(16)) negator_1 (.in(A), .out(negator_1_out));
  Comparator #(.width(16)) comparator_1 (.a(A), .b({16{1'b0}}), .lt(comparator_1_lt));  // open: gt, eq
  Negator #(.width(16)) negator_2 (.in(B), .out(negator_2_out));
  Comparator #(.width(16)) comparator_2 (.a(B), .b({16{1'b0}}), .eq(DIVOVER), .lt(comparator_2_lt));  // open: gt
  Multiplexer #(.select(3), .width(16), .enable("false")) multiplexer_1 (
    .in0({16{1'b0}}), .in1(REST), .in2(DIV), .in3({16{1'b0}}), .in4({16{1'b0}}), .in5(SOMA), .in6(SUB),
    .in7(MULT), .out(SAIDA), .sel(SELECT));
  Multiplexer #(.width(16), .enable("false")) multiplexer_2 (
    .in0(A), .in1(negator_1_out), .out(multiplexer_2_out), .sel(comparator_1_lt));
  Multiplexer #(.width(16), .enable("false")) multiplexer_3 (
    .in0(B), .in1(negator_2_out), .out(multiplexer_3_out), .sel(comparator_2_lt));
  and and_1 (and_1_out, comparator_1_lt, comparator_2_lt);
  Divider #(.width(16)) divider_1 (
    .a(multiplexer_2_out), .b(multiplexer_3_out), .out(divider_1_out), .rem(divider_1_rem));  // open: upper
  Subtractor #(.width(16)) subtractor_1 (.a(A), .b(B), .out(SUB), .bout(SUBOVER));  // open: bin
  Multiplier #(.width(16)) multiplier_1 (
    .a(multiplexer_2_out), .b(multiplexer_3_out), .out(multiplier_1_out), .cout(multiplier_1_cout));  // open: cin
  Adder #(.width(16)) adder_1 (.a(A), .b(B), .out(SOMA), .cout(SOMAOVER));  // open: cin
  Multiplexer #(.select(3), .enable("false")) multiplexer_4 (
    .in0(1'b0), .in1(DIVOVER), .in2(DIVOVER), .in3(1'b0), .in4(1'b0), .in5(SOMAOVER), .in6(1'b0),
    .in7(MULTOVER), .out(OVERFLOW), .sel(SELECT));
  Negator #(.width(16)) negator_3 (.in(divider_1_out), .out(negator_3_out));
  Negator #(.width(16)) negator_4 (.in(divider_1_rem), .out(negator_4_out));
  Negator #(.width(16)) negator_5 (.in(multiplier_1_out), .out(negator_5_out));
  Multiplexer #(.width(16), .enable("false")) multiplexer_5 (
    .in0(divider_1_out), .in1(negator_3_out), .out(DIV), .sel(and_1_out));
  Multiplexer #(.width(16), .enable("false")) multiplexer_6 (
    .in0(divider_1_rem), .in1(negator_4_out), .out(REST), .sel(and_1_out));
  Multiplexer #(.width(16), .enable("false")) multiplexer_7 (
    .in0(multiplier_1_out), .in1(negator_5_out), .out(MULT), .sel(and_1_out));
  or or_1 (MULTOVER, multiplier_1_cout[0], multiplier_1_cout[1], multiplier_1_cout[2], multiplier_1_cout[3], multiplier_1_cout[4], multiplier_1_cout[5], multiplier_1_cout[6], multiplier_1_cout[7], multiplier_1_cout[8], multiplier_1_cout[9], multiplier_1_cout[10], multiplier_1_cout[11], multiplier_1_cout[12], multiplier_1_cout[13], multiplier_1_cout[14], multiplier_1_cout[15]);
endmodule

module Control (
);

  wire [7:0] Controle;

  IsEqual8 isequal8_1 (.in_1(Controle), .in_2(8'hb));  // open: out_3
  IsEqual8 isequal8_2 (.in_1(Controle), .in_2(8'hc));  // open: out_3
  IsEqual8 isequal8_3 (.in_1(Controle), .in_2(8'h1b));  // open: out_3
  IsEqual8 isequal8_4 (.in_1(Controle), .in_2(8'h46));  // open: out_3
  IsEqual8 isequal8_5 (.in_1(Controle), .in_2(8'h15));  // open: out_3
  IsEqual8 isequal8_6 (.in_1(Controle), .in_2(8'h16));  // open: out_3
  IsEqual8 isequal8_7 (.in_1(Controle), .in_2(8'h17));  // open: out_3
  IsEqual8 isequal8_8 (.in_1(Controle), .in_2(8'h18));  // open: out_3
  IsEqual8 isequal8_9 (.in_1(Controle), .in_2(8'h19));  // open: out_3
  IsEqual8 isequal8_10 (.in_1(Controle), .in_2(8'h34));  // open: out_3
  IsEqual8 isequal8_11 (.in_1(Controle), .in_2(8'h35));  // open: out_3
  IsEqual8 isequal8_12 (.in_1(Controle), .in_2(8'h36));  // open: out_3
  IsEqual8 isequal8_13 (.in_1(Controle), .in_2(8'h37));  // open: out_3
  IsEqual8 isequal8_14 (.in_1(Controle), .in_2(8'h38));  // open: out_3
  IsEqual8 isequal8_15 (.in_1(Controle), .in_2(8'h39));  // open: out_3

  // Notes on the sheet:
  //   Carrega dado do endereço AB no acumulador
  //   Carrega acumulador no endereço AB
  //   Salto não condicional para AB
  //   Fim de execução
  //   Soma ACC com conteúdo do endereço XY
  //   Subtrai conteúdo do endereço XY de ACC
  //   Multiplica ACC pelo conteudo do endereco XY
  //   Divide ACC pelo conteudo do endereco XY
  //   Resto da divis˜ao de ACC pelo conteudo do endereco XY
  //   Desvia para  XY se ACC  menor ou igual a zero
  //   Idem, diferente de zero
  //   Idem, maior que zero
  //   Idem, igual a zero
  //   Idem, menor que zero
  //   Idem, maior ou igual a zero
endmodule
