// Logisim project MultLib.circ as structural Verilog: 1 circuit, main circuit main
module main (
  input  [7:0] In,
  input  [7:0] In_2,
  output [7:0] out_3,
  output Overflow
);

  wire and_1_out, and_2_out, and_3_out, and_4_out, and_5_out, and_6_out, and_7_out, and_8_out, and_9_out,
       and_10_out, and_11_out, and_12_out, and_13_out, and_14_out, and_15_out, and_16_out, and_17_out,
       and_18_out, and_19_out, and_20_out, and_21_out, and_22_out, and_23_out, and_24_out, and_25_out,
       and_26_out, and_27_out, and_28_out, and_29_out, and_30_out, and_31_out, and_32_out, and_33_out,
       and_34_out, and_35_out, and_36_out, and_37_out, and_38_out, and_39_out, and_40_out, and_41_out,
       and_42_out, and_43_out, and_44_out, and_45_out, and_46_out, and_47_out, and_48_out, and_49_out,
       and_50_out, and_51_out, and_52_out, and_53_out, and_54_out, and_55_out, and_56_out, and_57_out,
       and_58_out, and_59_out, and_60_out, and_61_out, and_62_out, and_63_out, soma1bit_1_out,
       soma1bit_2_out, soma1bit_3_carry_out, soma1bit_3_out, soma1bit_4_out, soma1bit_5_carry_out,
       soma1bit_5_out, soma1bit_6_carry_out, soma1bit_6_out, soma1bit_7_out, soma1bit_8_carry_out,
       soma1bit_8_out, soma1bit_9_carry_out, soma1bit_9_out, soma1bit_10_carry_out, soma1bit_10_out,
       soma1bit_11_out, soma1bit_12_carry_out, soma1bit_12_out, soma1bit_13_carry_out, soma1bit_13_out,
       soma1bit_14_carry_out, soma1bit_14_out, soma1bit_15_carry_out, soma1bit_15_out, soma1bit_16_out,
       soma1bit_17_out, soma1bit_18_carry_out, soma1bit_18_out, soma1bit_19_carry_out, soma1bit_19_out,
       soma1bit_20_carry_out, soma1bit_20_out, soma1bit_21_carry_out, soma1bit_21_out, soma1bit_22_carry_out,
       soma1bit_22_out, soma1bit_23_carry_out, soma1bit_23_out, soma1bit_24_carry_out, soma1bit_24_out,
       soma1bit_25_carry_out, soma1bit_25_out, soma1bit_26_carry_out, soma1bit_26_out, soma1bit_27_carry_out,
       soma1bit_27_out, soma1bit_28_carry_out, soma1bit_28_out, soma1bit_29_carry_out, soma1bit_29_out,
       soma1bit_30_carry_out, soma1bit_30_out, soma1bit_31_carry_out, soma1bit_31_out, soma1bit_32_carry_out,
       soma1bit_32_out, soma1bit_33_carry_out, soma1bit_33_out, soma1bit_34_carry_out, soma1bit_35_carry_out,
       soma1bit_35_out, soma1bit_36_carry_out, soma1bit_36_out, soma1bit_37_carry_out, soma1bit_37_out,
       soma1bit_38_carry_out, soma1bit_38_out, soma1bit_39_carry_out, soma1bit_39_out, soma1bit_40_carry_out,
       soma1bit_40_out, soma1bit_41_carry_out, soma1bit_42_carry_out, soma1bit_42_out, soma1bit_43_carry_out,
       soma1bit_43_out, soma1bit_44_carry_out, soma1bit_44_out, soma1bit_45_carry_out, soma1bit_45_out,
       soma1bit_46_carry_out, soma1bit_47_carry_out, soma1bit_47_out, soma1bit_48_carry_out, soma1bit_48_out,
       soma1bit_49_carry_out, soma1bit_49_out, soma1bit_50_carry_out, soma1bit_51_carry_out, soma1bit_51_out,
       soma1bit_52_carry_out, soma1bit_52_out, soma1bit_53_carry_out, soma1bit_54_carry_out, soma1bit_54_out,
       soma1bit_55_carry_out, soma1bit_56_carry_out;

  and and_1 (and_1_out, In[7], In_2[7]);
  Soma1bit soma1bit_1 (
    .Bit1(and_1_out), .Bit2(1'b0), .Out(soma1bit_1_out), .Carry_In(soma1bit_3_carry_out));  // open: Carry_Out
  and and_2 (and_2_out, In[7], In_2[6]);
  Soma1bit soma1bit_2 (
    .Bit1(and_2_out), .Bit2(1'b0), .Out(soma1bit_2_out), .Carry_In(soma1bit_5_carry_out));  // open: Carry_Out
  and and_3 (and_3_out, In[6], In_2[7]);
  Soma1bit soma1bit_3 (
    .Bit1(and_3_out), .Bit2(soma1bit_2_out), .Out(soma1bit_3_out), .Carry_In(soma1bit_6_carry_out),
    .Carry_Out(soma1bit_3_carry_out));
  and and_4 (and_4_out, In[7], In_2[5]);
  Soma1bit soma1bit_4 (
    .Bit1(and_4_out), .Bit2(1'b0), .Out(soma1bit_4_out), .Carry_In(soma1bit_8_carry_out));  // open: Carry_Out
  and and_5 (and_5_out, In[6], In_2[6]);
  Soma1bit soma1bit_5 (
    .Bit1(and_5_out), .Bit2(soma1bit_4_out), .Out(soma1bit_5_out), .Carry_In(soma1bit_9_carry_out),
    .Carry_Out(soma1bit_5_carry_out));
  and and_6 (and_6_out, In[5], In_2[7]);
  Soma1bit soma1bit_6 (
    .Bit1(and_6_out), .Bit2(soma1bit_5_out), .Out(soma1bit_6_out), .Carry_In(soma1bit_10_carry_out),
    .Carry_Out(soma1bit_6_carry_out));
  and and_7 (and_7_out, In[7], In_2[4]);
  Soma1bit soma1bit_7 (
    .Bit1(and_7_out), .Bit2(1'b0), .Out(soma1bit_7_out), .Carry_In(soma1bit_12_carry_out));  // open: Carry_Out
  and and_8 (and_8_out, In[6], In_2[5]);
  Soma1bit soma1bit_8 (
    .Bit1(and_8_out), .Bit2(soma1bit_7_out), .Out(soma1bit_8_out), .Carry_In(soma1bit_13_carry_out),
    .Carry_Out(soma1bit_8_carry_out));
  and and_9 (and_9_out, In[5], In_2[6]);
  Soma1bit soma1bit_9 (
    .Bit1(and_9_out), .Bit2(soma1bit_8_out), .Out(soma1bit_9_out), .Carry_In(soma1bit_14_carry_out),
    .Carry_Out(soma1bit_9_carry_out));
  and and_10 (and_10_out, In[4], In_2[7]);
  Soma1bit soma1bit_10 (
    .Bit1(and_10_out), .Bit2(soma1bit_9_out), .Out(soma1bit_10_out), .Carry_In(soma1bit_15_carry_out),
    .Carry_Out(soma1bit_10_carry_out));
  or or_1 (Overflow, soma1bit_1_out, soma1bit_3_out, soma1bit_6_out, soma1bit_10_out, soma1bit_15_out, soma1bit_22_out, soma1bit_35_out, out_3[7]);
  and and_11 (and_11_out, In[7], In_2[3]);
  Soma1bit soma1bit_11 (
    .Bit1(and_11_out), .Bit2(1'b0), .Out(soma1bit_11_out), .Carry_In(soma1bit_18_carry_out));  // open: Carry_Out
  and and_12 (and_12_out, In[6], In_2[4]);
  Soma1bit soma1bit_12 (
    .Bit1(and_12_out), .Bit2(soma1bit_11_out), .Out(soma1bit_12_out), .Carry_In(soma1bit_19_carry_out),
    .Carry_Out(soma1bit_12_carry_out));
  and and_13 (and_13_out, In[5], In_2[5]);
  Soma1bit soma1bit_13 (
    .Bit1(and_13_out), .Bit2(soma1bit_12_out), .Out(soma1bit_13_out), .Carry_In(soma1bit_20_carry_out),
    .Carry_Out(soma1bit_13_carry_out));
  and and_14 (and_14_out, In[4], In_2[6]);
  Soma1bit soma1bit_14 (
    .Bit1(and_14_out), .Bit2(soma1bit_13_out), .Out(soma1bit_14_out), .Carry_In(soma1bit_21_carry_out),
    .Carry_Out(soma1bit_14_carry_out));
  and and_15 (and_15_out, In[3], In_2[7]);
  Soma1bit soma1bit_15 (
    .Bit1(and_15_out), .Bit2(soma1bit_14_out), .Out(soma1bit_15_out), .Carry_In(soma1bit_22_carry_out),
    .Carry_Out(soma1bit_15_carry_out));
  and and_16 (and_16_out, In[7], In_2[1]);
  Soma1bit soma1bit_16 (
    .Bit1(and_16_out), .Bit2(1'b0), .Out(soma1bit_16_out), .Carry_In(soma1bit_23_carry_out));  // open: Carry_Out
  and and_17 (and_17_out, In[7], In_2[2]);
  Soma1bit soma1bit_17 (
    .Bit1(and_17_out), .Bit2(1'b0), .Out(soma1bit_17_out), .Carry_In(soma1bit_25_carry_out));  // open: Carry_Out
  and and_18 (and_18_out, In[6], In_2[3]);
  Soma1bit soma1bit_18 (
    .Bit1(and_18_out), .Bit2(soma1bit_17_out), .Out(soma1bit_18_out), .Carry_In(soma1bit_27_carry_out),
    .Carry_Out(soma1bit_18_carry_out));
  and and_19 (and_19_out, In[5], In_2[4]);
  Soma1bit soma1bit_19 (
    .Bit1(and_19_out), .Bit2(soma1bit_18_out), .Out(soma1bit_19_out), .Carry_In(soma1bit_28_carry_out),
    .Carry_Out(soma1bit_19_carry_out));
  and and_20 (and_20_out, In[4], In_2[5]);
  Soma1bit soma1bit_20 (
    .Bit1(and_20_out), .Bit2(soma1bit_19_out), .Out(soma1bit_20_out), .Carry_In(soma1bit_31_carry_out),
    .Carry_Out(soma1bit_20_carry_out));
  and and_21 (and_21_out, In[3], In_2[6]);
  Soma1bit soma1bit_21 (
    .Bit1(and_21_out), .Bit2(soma1bit_20_out), .Out(soma1bit_21_out), .Carry_In(soma1bit_32_carry_out),
    .Carry_Out(soma1bit_21_carry_out));
  and and_22 (and_22_out, In[2], In_2[7]);
  Soma1bit soma1bit_22 (
    .Bit1(and_22_out), .Bit2(soma1bit_21_out), .Out(soma1bit_22_out), .Carry_In(soma1bit_35_carry_out),
    .Carry_Out(soma1bit_22_carry_out));
  and and_23 (and_23_out, In[7], In_2[0]);
  and and_24 (and_24_out, In[6], In_2[1]);
  Soma1bit soma1bit_23 (
    .Bit1(and_24_out), .Bit2(and_23_out), .Out(soma1bit_23_out), .Carry_In(soma1bit_36_carry_out),
    .Carry_Out(soma1bit_23_carry_out));
  and and_25 (and_25_out, In[6], In_2[2]);
  and and_26 (and_26_out, In[5], In_2[2]);
  Soma1bit soma1bit_24 (
    .Bit1(and_26_out), .Bit2(soma1bit_23_out), .Out(soma1bit_24_out), .Carry_In(soma1bit_37_carry_out),
    .Carry_Out(soma1bit_24_carry_out));
  Soma1bit soma1bit_25 (
    .Bit1(and_25_out), .Bit2(soma1bit_16_out), .Out(soma1bit_25_out), .Carry_In(soma1bit_24_carry_out),
    .Carry_Out(soma1bit_25_carry_out));
  and and_27 (and_27_out, In[4], In_2[3]);
  and and_28 (and_28_out, In[5], In_2[3]);
  Soma1bit soma1bit_26 (
    .Bit1(and_27_out), .Bit2(soma1bit_24_out), .Out(soma1bit_26_out), .Carry_In(soma1bit_38_carry_out),
    .Carry_Out(soma1bit_26_carry_out));
  Soma1bit soma1bit_27 (
    .Bit1(and_28_out), .Bit2(soma1bit_25_out), .Out(soma1bit_27_out), .Carry_In(soma1bit_26_carry_out),
    .Carry_Out(soma1bit_27_carry_out));
  and and_29 (and_29_out, In[4], In_2[4]);
  and and_30 (and_30_out, In[3], In_2[4]);
  Soma1bit soma1bit_28 (
    .Bit1(and_29_out), .Bit2(soma1bit_27_out), .Out(soma1bit_28_out), .Carry_In(soma1bit_29_carry_out),
    .Carry_Out(soma1bit_28_carry_out));
  Soma1bit soma1bit_29 (
    .Bit1(and_30_out), .Bit2(soma1bit_26_out), .Out(soma1bit_29_out), .Carry_In(soma1bit_39_carry_out),
    .Carry_Out(soma1bit_29_carry_out));
  and and_31 (and_31_out, In[3], In_2[5]);
  and and_32 (and_32_out, In[2], In_2[5]);
  Soma1bit soma1bit_30 (
    .Bit1(and_32_out), .Bit2(soma1bit_29_out), .Out(soma1bit_30_out), .Carry_In(soma1bit_40_carry_out),
    .Carry_Out(soma1bit_30_carry_out));
  Soma1bit soma1bit_31 (
    .Bit1(and_31_out), .Bit2(soma1bit_28_out), .Out(soma1bit_31_out), .Carry_In(soma1bit_30_carry_out),
    .Carry_Out(soma1bit_31_carry_out));
  and and_33 (and_33_out, In[1], In_2[6]);
  and and_34 (and_34_out, In[2], In_2[6]);
  Soma1bit soma1bit_32 (
    .Bit1(and_34_out), .Bit2(soma1bit_31_out), .Out(soma1bit_32_out), .Carry_In(soma1bit_33_carry_out),
    .Carry_Out(soma1bit_32_carry_out));
  Soma1bit soma1bit_33 (
    .Bit1(and_33_out), .Bit2(soma1bit_30_out), .Out(soma1bit_33_out), .Carry_In(soma1bit_41_carry_out),
    .Carry_Out(soma1bit_33_carry_out));
  and and_35 (and_35_out, In[1], In_2[7]);
  and and_36 (and_36_out, In[0], In_2[7]);
  Soma1bit soma1bit_34 (
    .Bit1(and_36_out), .Bit2(soma1bit_33_out), .Out(out_3[7]), .Carry_In(1'b0),
    .Carry_Out(soma1bit_34_carry_out));
  Soma1bit soma1bit_35 (
    .Bit1(and_35_out), .Bit2(soma1bit_32_out), .Out(soma1bit_35_out), .Carry_In(soma1bit_34_carry_out),
    .Carry_Out(soma1bit_35_carry_out));
  and and_37 (and_37_out, In[6], In_2[0]);
  and and_38 (and_38_out, In[5], In_2[1]);
  Soma1bit soma1bit_36 (
    .Bit1(and_38_out), .Bit2(and_37_out), .Out(soma1bit_36_out), .Carry_In(soma1bit_42_carry_out),
    .Carry_Out(soma1bit_36_carry_out));
  and and_39 (and_39_out, In[4], In_2[2]);
  Soma1bit soma1bit_37 (
    .Bit1(and_39_out), .Bit2(soma1bit_36_out), .Out(soma1bit_37_out), .Carry_In(soma1bit_43_carry_out),
    .Carry_Out(soma1bit_37_carry_out));
  and and_40 (and_40_out, In[3], In_2[3]);
  Soma1bit soma1bit_38 (
    .Bit1(and_40_out), .Bit2(soma1bit_37_out), .Out(soma1bit_38_out), .Carry_In(soma1bit_44_carry_out),
    .Carry_Out(soma1bit_38_carry_out));
  and and_41 (and_41_out, In[2], In_2[4]);
  Soma1bit soma1bit_39 (
    .Bit1(and_41_out), .Bit2(soma1bit_38_out), .Out(soma1bit_39_out), .Carry_In(soma1bit_45_carry_out),
    .Carry_Out(soma1bit_39_carry_out));
  and and_42 (and_42_out, In[1], In_2[5]);
  Soma1bit soma1bit_40 (
    .Bit1(and_42_out), .Bit2(soma1bit_39_out), .Out(soma1bit_40_out), .Carry_In(soma1bit_46_carry_out),
    .Carry_Out(soma1bit_40_carry_out));
  and and_43 (and_43_out, In[0], In_2[6]);
  Soma1bit soma1bit_41 (
    .Bit1(and_43_out), .Bit2(soma1bit_40_out), .Out(out_3[6]), .Carry_In(1'b0),
    .Carry_Out(soma1bit_41_carry_out));
  and and_44 (and_44_out, In[5], In_2[0]);
  and and_45 (and_45_out, In[4], In_2[1]);
  Soma1bit soma1bit_42 (
    .Bit1(and_45_out), .Bit2(and_44_out), .Out(soma1bit_42_out), .Carry_In(soma1bit_47_carry_out),
    .Carry_Out(soma1bit_42_carry_out));
  and and_46 (and_46_out, In[3], In_2[2]);
  Soma1bit soma1bit_43 (
    .Bit1(and_46_out), .Bit2(soma1bit_42_out), .Out(soma1bit_43_out), .Carry_In(soma1bit_48_carry_out),
    .Carry_Out(soma1bit_43_carry_out));
  and and_47 (and_47_out, In[2], In_2[3]);
  Soma1bit soma1bit_44 (
    .Bit1(and_47_out), .Bit2(soma1bit_43_out), .Out(soma1bit_44_out), .Carry_In(soma1bit_49_carry_out),
    .Carry_Out(soma1bit_44_carry_out));
  and and_48 (and_48_out, In[1], In_2[4]);
  Soma1bit soma1bit_45 (
    .Bit1(and_48_out), .Bit2(soma1bit_44_out), .Out(soma1bit_45_out), .Carry_In(soma1bit_50_carry_out),
    .Carry_Out(soma1bit_45_carry_out));
  and and_49 (and_49_out, In[0], In_2[5]);
  Soma1bit soma1bit_46 (
    .Bit1(and_49_out), .Bit2(soma1bit_45_out), .Out(out_3[5]), .Carry_In(1'b0),
    .Carry_Out(soma1bit_46_carry_out));
  and and_50 (and_50_out, In[4], In_2[0]);
  and and_51 (and_51_out, In[3], In_2[1]);
  Soma1bit soma1bit_47 (
    .Bit1(and_51_out), .Bit2(and_50_out), .Out(soma1bit_47_out), .Carry_In(soma1bit_51_carry_out),
    .Carry_Out(soma1bit_47_carry_out));
  and and_52 (and_52_out, In[2], In_2[2]);
  Soma1bit soma1bit_48 (
    .Bit1(and_52_out), .Bit2(soma1bit_47_out), .Out(soma1bit_48_out), .Carry_In(soma1bit_52_carry_out),
    .Carry_Out(soma1bit_48_carry_out));
  and and_53 (and_53_out, In[1], In_2[3]);
  Soma1bit soma1bit_49 (
    .Bit1(and_53_out), .Bit2(soma1bit_48_out), .Out(soma1bit_49_out), .Carry_In(soma1bit_53_carry_out),
    .Carry_Out(soma1bit_49_carry_out));
  and and_54 (and_54_out, In[0], In_2[4]);
  Soma1bit soma1bit_50 (
    .Bit1(and_54_out), .Bit2(soma1bit_49_out), .Out(out_3[4]), .Carry_In(1'b0),
    .Carry_Out(soma1bit_50_carry_out));
  and and_55 (and_55_out, In[3], In_2[0]);
  and and_56 (and_56_out, In[2], In_2[1]);
  Soma1bit soma1bit_51 (
    .Bit1(and_56_out), .Bit2(and_55_out), .Out(soma1bit_51_out), .Carry_In(soma1bit_54_carry_out),
    .Carry_Out(soma1bit_51_carry_out));
  and and_57 (and_57_out, In[1], In_2[2]);
  Soma1bit soma1bit_52 (
    .Bit1(and_57_out), .Bit2(soma1bit_51_out), .Out(soma1bit_52_out), .Carry_In(soma1bit_55_carry_out),
    .Carry_Out(soma1bit_52_carry_out));
  and and_58 (and_58_out, In[0], In_2[3]);
  Soma1bit soma1bit_53 (
    .Bit1(and_58_out), .Bit2(soma1bit_52_out), .Out(out_3[3]), .Carry_In(1'b0),
    .Carry_Out(soma1bit_53_carry_out));
  and and_59 (and_59_out, In[2], In_2[0]);
  and and_60 (and_60_out, In[1], In_2[1]);
  Soma1bit soma1bit_54 (
    .Bit1(and_60_out), .Bit2(and_59_out), .Out(soma1bit_54_out), .Carry_In(soma1bit_56_carry_out),
    .Carry_Out(soma1bit_54_carry_out));
  and and_61 (and_61_out, In[0], In_2[2]);
  Soma1bit soma1bit_55 (
    .Bit1(and_61_out), .Bit2(soma1bit_54_out), .Out(out_3[2]), .Carry_In(1'b0),
    .Carry_Out(soma1bit_55_carry_out));
  and and_62 (and_62_out, In[1], In_2[0]);
  and and_63 (and_63_out, In[0], In_2[1]);
  Soma1bit soma1bit_56 (
    .Bit1(and_63_out), .Bit2(and_62_out), .Out(out_3[1]), .Carry_In(1'b0), .Carry_Out(soma1bit_56_carry_out));
  and and_64 (out_3[0], In[0], In_2[0]);
endmodule
