// Logisim project QuociLib.circ as structural Verilog
module main (
  input  [7:0] B,
  input  [7:0] A,
  output [7:0] A_B,
  output [7:0] A_B_2
);

  wire divblock_2_d___x_y, divblock_2_l_o, divblock_4_d___x_y, divblock_4_l_o, divblock_5_d___x_y,
       divblock_5_l_o, divblock_7_d___x_y, divblock_7_l_o, divblock_8_d___x_y, divblock_8_l_o,
       divblock_9_d___x_y, divblock_9_l_o, divblock_11_d___x_y, divblock_11_l_o, divblock_12_d___x_y,
       divblock_12_l_o, divblock_13_d___x_y, divblock_13_l_o, divblock_14_d___x_y, divblock_14_l_o,
       divblock_16_d___x_y, divblock_16_l_o, divblock_17_d___x_y, divblock_17_l_o, divblock_18_d___x_y,
       divblock_18_l_o, divblock_19_d___x_y, divblock_19_l_o, divblock_20_d___x_y, divblock_20_l_o,
       divblock_22_d___x_y, divblock_22_l_o, divblock_23_d___x_y, divblock_23_l_o, divblock_24_d___x_y,
       divblock_24_l_o, divblock_25_d___x_y, divblock_25_l_o, divblock_26_d___x_y, divblock_26_l_o,
       divblock_27_d___x_y, divblock_27_l_o, divblock_29_d___x_y, divblock_29_l_o, divblock_30_d___x_y,
       divblock_30_l_o, divblock_31_d___x_y, divblock_31_l_o, divblock_32_d___x_y, divblock_32_l_o,
       divblock_33_d___x_y, divblock_33_l_o, divblock_34_d___x_y, divblock_34_l_o, divblock_35_d___x_y,
       divblock_35_l_o, divblock_37_d___x_y, divblock_37_l_o, divblock_38_d___x_y, divblock_38_l_o,
       divblock_39_d___x_y, divblock_39_l_o, divblock_40_d___x_y, divblock_40_l_o, divblock_41_d___x_y,
       divblock_41_l_o, divblock_42_d___x_y, divblock_42_l_o, divblock_43_l_o, divblock_44_d___x_y,
       divblock_44_l_o, divblock_45_d___x_y, divblock_45_l_o, divblock_46_d___x_y, divblock_46_l_o,
       divblock_47_d___x_y, divblock_47_l_o, divblock_48_d___x_y, divblock_48_l_o, divblock_49_l_o,
       divblock_50_d___x_y, divblock_50_l_o, divblock_51_d___x_y, divblock_51_l_o, divblock_52_d___x_y,
       divblock_52_l_o, divblock_53_d___x_y, divblock_53_l_o, divblock_54_l_o, divblock_55_d___x_y,
       divblock_55_l_o, divblock_56_d___x_y, divblock_56_l_o, divblock_57_d___x_y, divblock_57_l_o,
       divblock_58_l_o, divblock_59_d___x_y, divblock_59_l_o, divblock_60_d___x_y, divblock_60_l_o,
       divblock_61_l_o, divblock_62_d___x_y, divblock_62_l_o, divblock_63_l_o, divblock_64_l_o, S0, S1, S2,
       S3, S4, S5, S6, S7;

  not not_1 (A_B[7], S0);
  DivBlock divblock_1 (.Y(B[7]), .X(1'b0), .L_o(S0), .OS(S0), .L_i(divblock_2_l_o));  // open: D___X_Y
  not not_2 (A_B[6], S1);
  DivBlock divblock_2 (
    .Y(B[6]), .X(1'b0), .L_o(divblock_2_l_o), .OS(S0), .D___X_Y(divblock_2_d___x_y), .L_i(divblock_4_l_o));
  DivBlock divblock_3 (.Y(B[7]), .X(divblock_2_d___x_y), .L_o(S1), .OS(S1), .L_i(divblock_5_l_o));  // open: D___X_Y
  not not_3 (A_B[5], S2);
  DivBlock divblock_4 (
    .Y(B[5]), .X(1'b0), .L_o(divblock_4_l_o), .OS(S0), .D___X_Y(divblock_4_d___x_y), .L_i(divblock_7_l_o));
  DivBlock divblock_5 (
    .Y(B[6]), .X(divblock_4_d___x_y), .L_o(divblock_5_l_o), .OS(S1), .D___X_Y(divblock_5_d___x_y),
    .L_i(divblock_8_l_o));
  DivBlock divblock_6 (.Y(B[7]), .X(divblock_5_d___x_y), .L_o(S2), .OS(S2), .L_i(divblock_9_l_o));  // open: D___X_Y
  not not_4 (A_B[4], S3);
  DivBlock divblock_7 (
    .Y(B[4]), .X(1'b0), .L_o(divblock_7_l_o), .OS(S0), .D___X_Y(divblock_7_d___x_y), .L_i(divblock_11_l_o));
  DivBlock divblock_8 (
    .Y(B[5]), .X(divblock_7_d___x_y), .L_o(divblock_8_l_o), .OS(S1), .D___X_Y(divblock_8_d___x_y),
    .L_i(divblock_12_l_o));
  DivBlock divblock_9 (
    .Y(B[6]), .X(divblock_8_d___x_y), .L_o(divblock_9_l_o), .OS(S2), .D___X_Y(divblock_9_d___x_y),
    .L_i(divblock_13_l_o));
  DivBlock divblock_10 (.Y(B[7]), .X(divblock_9_d___x_y), .L_o(S3), .OS(S3), .L_i(divblock_14_l_o));  // open: D___X_Y
  not not_5 (A_B[3], S4);
  DivBlock divblock_11 (
    .Y(B[3]), .X(1'b0), .L_o(divblock_11_l_o), .OS(S0), .D___X_Y(divblock_11_d___x_y), .L_i(divblock_16_l_o));
  DivBlock divblock_12 (
    .Y(B[4]), .X(divblock_11_d___x_y), .L_o(divblock_12_l_o), .OS(S1), .D___X_Y(divblock_12_d___x_y),
    .L_i(divblock_17_l_o));
  DivBlock divblock_13 (
    .Y(B[5]), .X(divblock_12_d___x_y), .L_o(divblock_13_l_o), .OS(S2), .D___X_Y(divblock_13_d___x_y),
    .L_i(divblock_18_l_o));
  DivBlock divblock_14 (
    .Y(B[6]), .X(divblock_13_d___x_y), .L_o(divblock_14_l_o), .OS(S3), .D___X_Y(divblock_14_d___x_y),
    .L_i(divblock_19_l_o));
  DivBlock divblock_15 (.Y(B[7]), .X(divblock_14_d___x_y), .L_o(S4), .OS(S4), .L_i(divblock_20_l_o));  // open: D___X_Y
  not not_6 (A_B[2], S5);
  DivBlock divblock_16 (
    .Y(B[2]), .X(1'b0), .L_o(divblock_16_l_o), .OS(S0), .D___X_Y(divblock_16_d___x_y), .L_i(divblock_22_l_o));
  DivBlock divblock_17 (
    .Y(B[3]), .X(divblock_16_d___x_y), .L_o(divblock_17_l_o), .OS(S1), .D___X_Y(divblock_17_d___x_y),
    .L_i(divblock_23_l_o));
  DivBlock divblock_18 (
    .Y(B[4]), .X(divblock_17_d___x_y), .L_o(divblock_18_l_o), .OS(S2), .D___X_Y(divblock_18_d___x_y),
    .L_i(divblock_24_l_o));
  DivBlock divblock_19 (
    .Y(B[5]), .X(divblock_18_d___x_y), .L_o(divblock_19_l_o), .OS(S3), .D___X_Y(divblock_19_d___x_y),
    .L_i(divblock_25_l_o));
  DivBlock divblock_20 (
    .Y(B[6]), .X(divblock_19_d___x_y), .L_o(divblock_20_l_o), .OS(S4), .D___X_Y(divblock_20_d___x_y),
    .L_i(divblock_26_l_o));
  DivBlock divblock_21 (.Y(B[7]), .X(divblock_20_d___x_y), .L_o(S5), .OS(S5), .L_i(divblock_27_l_o));  // open: D___X_Y
  not not_7 (A_B[1], S6);
  DivBlock divblock_22 (
    .Y(B[1]), .X(1'b0), .L_o(divblock_22_l_o), .OS(S0), .D___X_Y(divblock_22_d___x_y), .L_i(divblock_29_l_o));
  DivBlock divblock_23 (
    .Y(B[2]), .X(divblock_22_d___x_y), .L_o(divblock_23_l_o), .OS(S1), .D___X_Y(divblock_23_d___x_y),
    .L_i(divblock_30_l_o));
  DivBlock divblock_24 (
    .Y(B[3]), .X(divblock_23_d___x_y), .L_o(divblock_24_l_o), .OS(S2), .D___X_Y(divblock_24_d___x_y),
    .L_i(divblock_31_l_o));
  DivBlock divblock_25 (
    .Y(B[4]), .X(divblock_24_d___x_y), .L_o(divblock_25_l_o), .OS(S3), .D___X_Y(divblock_25_d___x_y),
    .L_i(divblock_32_l_o));
  DivBlock divblock_26 (
    .Y(B[5]), .X(divblock_25_d___x_y), .L_o(divblock_26_l_o), .OS(S4), .D___X_Y(divblock_26_d___x_y),
    .L_i(divblock_33_l_o));
  DivBlock divblock_27 (
    .Y(B[6]), .X(divblock_26_d___x_y), .L_o(divblock_27_l_o), .OS(S5), .D___X_Y(divblock_27_d___x_y),
    .L_i(divblock_34_l_o));
  DivBlock divblock_28 (.Y(B[7]), .X(divblock_27_d___x_y), .L_o(S6), .OS(S6), .L_i(divblock_35_l_o));  // open: D___X_Y
  not not_8 (A_B[0], S7);
  DivBlock divblock_29 (.Y(B[0]), .X(A[7]), .L_o(divblock_29_l_o), .OS(S0), .D___X_Y(divblock_29_d___x_y), .L_i(1'b0));
  DivBlock divblock_30 (
    .Y(B[1]), .X(divblock_29_d___x_y), .L_o(divblock_30_l_o), .OS(S1), .D___X_Y(divblock_30_d___x_y),
    .L_i(divblock_37_l_o));
  DivBlock divblock_31 (
    .Y(B[2]), .X(divblock_30_d___x_y), .L_o(divblock_31_l_o), .OS(S2), .D___X_Y(divblock_31_d___x_y),
    .L_i(divblock_38_l_o));
  DivBlock divblock_32 (
    .Y(B[3]), .X(divblock_31_d___x_y), .L_o(divblock_32_l_o), .OS(S3), .D___X_Y(divblock_32_d___x_y),
    .L_i(divblock_39_l_o));
  DivBlock divblock_33 (
    .Y(B[4]), .X(divblock_32_d___x_y), .L_o(divblock_33_l_o), .OS(S4), .D___X_Y(divblock_33_d___x_y),
    .L_i(divblock_40_l_o));
  DivBlock divblock_34 (
    .Y(B[5]), .X(divblock_33_d___x_y), .L_o(divblock_34_l_o), .OS(S5), .D___X_Y(divblock_34_d___x_y),
    .L_i(divblock_41_l_o));
  DivBlock divblock_35 (
    .Y(B[6]), .X(divblock_34_d___x_y), .L_o(divblock_35_l_o), .OS(S6), .D___X_Y(divblock_35_d___x_y),
    .L_i(divblock_42_l_o));
  DivBlock divblock_36 (
    .Y(B[7]), .X(divblock_35_d___x_y), .L_o(S7), .OS(S7), .D___X_Y(A_B_2[7]), .L_i(divblock_43_l_o));
  DivBlock divblock_37 (.Y(B[0]), .X(A[6]), .L_o(divblock_37_l_o), .OS(S1), .D___X_Y(divblock_37_d___x_y), .L_i(1'b0));
  DivBlock divblock_38 (
    .Y(B[1]), .X(divblock_37_d___x_y), .L_o(divblock_38_l_o), .OS(S2), .D___X_Y(divblock_38_d___x_y),
    .L_i(divblock_44_l_o));
  DivBlock divblock_39 (
    .Y(B[2]), .X(divblock_38_d___x_y), .L_o(divblock_39_l_o), .OS(S3), .D___X_Y(divblock_39_d___x_y),
    .L_i(divblock_45_l_o));
  DivBlock divblock_40 (
    .Y(B[3]), .X(divblock_39_d___x_y), .L_o(divblock_40_l_o), .OS(S4), .D___X_Y(divblock_40_d___x_y),
    .L_i(divblock_46_l_o));
  DivBlock divblock_41 (
    .Y(B[4]), .X(divblock_40_d___x_y), .L_o(divblock_41_l_o), .OS(S5), .D___X_Y(divblock_41_d___x_y),
    .L_i(divblock_47_l_o));
  DivBlock divblock_42 (
    .Y(B[5]), .X(divblock_41_d___x_y), .L_o(divblock_42_l_o), .OS(S6), .D___X_Y(divblock_42_d___x_y),
    .L_i(divblock_48_l_o));
  DivBlock divblock_43 (
    .Y(B[6]), .X(divblock_42_d___x_y), .L_o(divblock_43_l_o), .OS(S7), .D___X_Y(A_B_2[6]),
    .L_i(divblock_49_l_o));
  DivBlock divblock_44 (.Y(B[0]), .X(A[5]), .L_o(divblock_44_l_o), .OS(S2), .D___X_Y(divblock_44_d___x_y), .L_i(1'b0));
  DivBlock divblock_45 (
    .Y(B[1]), .X(divblock_44_d___x_y), .L_o(divblock_45_l_o), .OS(S3), .D___X_Y(divblock_45_d___x_y),
    .L_i(divblock_50_l_o));
  DivBlock divblock_46 (
    .Y(B[2]), .X(divblock_45_d___x_y), .L_o(divblock_46_l_o), .OS(S4), .D___X_Y(divblock_46_d___x_y),
    .L_i(divblock_51_l_o));
  DivBlock divblock_47 (
    .Y(B[3]), .X(divblock_46_d___x_y), .L_o(divblock_47_l_o), .OS(S5), .D___X_Y(divblock_47_d___x_y),
    .L_i(divblock_52_l_o));
  DivBlock divblock_48 (
    .Y(B[4]), .X(divblock_47_d___x_y), .L_o(divblock_48_l_o), .OS(S6), .D___X_Y(divblock_48_d___x_y),
    .L_i(divblock_53_l_o));
  DivBlock divblock_49 (
    .Y(B[5]), .X(divblock_48_d___x_y), .L_o(divblock_49_l_o), .OS(S7), .D___X_Y(A_B_2[5]),
    .L_i(divblock_54_l_o));
  DivBlock divblock_50 (.Y(B[0]), .X(A[4]), .L_o(divblock_50_l_o), .OS(S3), .D___X_Y(divblock_50_d___x_y), .L_i(1'b0));
  DivBlock divblock_51 (
    .Y(B[1]), .X(divblock_50_d___x_y), .L_o(divblock_51_l_o), .OS(S4), .D___X_Y(divblock_51_d___x_y),
    .L_i(divblock_55_l_o));
  DivBlock divblock_52 (
    .Y(B[2]), .X(divblock_51_d___x_y), .L_o(divblock_52_l_o), .OS(S5), .D___X_Y(divblock_52_d___x_y),
    .L_i(divblock_56_l_o));
  DivBlock divblock_53 (
    .Y(B[3]), .X(divblock_52_d___x_y), .L_o(divblock_53_l_o), .OS(S6), .D___X_Y(divblock_53_d___x_y),
    .L_i(divblock_57_l_o));
  DivBlock divblock_54 (
    .Y(B[4]), .X(divblock_53_d___x_y), .L_o(divblock_54_l_o), .OS(S7), .D___X_Y(A_B_2[4]),
    .L_i(divblock_58_l_o));
  DivBlock divblock_55 (.Y(B[0]), .X(A[3]), .L_o(divblock_55_l_o), .OS(S4), .D___X_Y(divblock_55_d___x_y), .L_i(1'b0));
  DivBlock divblock_56 (
    .Y(B[1]), .X(divblock_55_d___x_y), .L_o(divblock_56_l_o), .OS(S5), .D___X_Y(divblock_56_d___x_y),
    .L_i(divblock_59_l_o));
  DivBlock divblock_57 (
    .Y(B[2]), .X(divblock_56_d___x_y), .L_o(divblock_57_l_o), .OS(S6), .D___X_Y(divblock_57_d___x_y),
    .L_i(divblock_60_l_o));
  DivBlock divblock_58 (
    .Y(B[3]), .X(divblock_57_d___x_y), .L_o(divblock_58_l_o), .OS(S7), .D___X_Y(A_B_2[3]),
    .L_i(divblock_61_l_o));
  DivBlock divblock_59 (.Y(B[0]), .X(A[2]), .L_o(divblock_59_l_o), .OS(S5), .D___X_Y(divblock_59_d___x_y), .L_i(1'b0));
  DivBlock divblock_60 (
    .Y(B[1]), .X(divblock_59_d___x_y), .L_o(divblock_60_l_o), .OS(S6), .D___X_Y(divblock_60_d___x_y),
    .L_i(divblock_62_l_o));
  DivBlock divblock_61 (
    .Y(B[2]), .X(divblock_60_d___x_y), .L_o(divblock_61_l_o), .OS(S7), .D___X_Y(A_B_2[2]),
    .L_i(divblock_63_l_o));
  DivBlock divblock_62 (.Y(B[0]), .X(A[1]), .L_o(divblock_62_l_o), .OS(S6), .D___X_Y(divblock_62_d___x_y), .L_i(1'b0));
  DivBlock divblock_63 (
    .Y(B[1]), .X(divblock_62_d___x_y), .L_o(divblock_63_l_o), .OS(S7), .D___X_Y(A_B_2[1]),
    .L_i(divblock_64_l_o));
  DivBlock divblock_64 (.Y(B[0]), .X(A[0]), .L_o(divblock_64_l_o), .OS(S7), .D___X_Y(A_B_2[0]), .L_i(1'b0));

  // Other names for the same wires on the sheet: Q0 = A_B[0]; Q1 = A_B[1]; Q2 = A_B[2]; Q3 = A_B[3]; Q4 = A_B[4];
  //   Q5 = A_B[5]; Q6 = A_B[6]; Q7 = A_B[7]; R0 = A_B_2[0]; R1 = A_B_2[1]; R2 = A_B_2[2]; R3 = A_B_2[3];
  //   R4 = A_B_2[4]; R5 = A_B_2[5]; R6 = A_B_2[6]; R7 = A_B_2[7]
endmodule

module DivBlock (
  input  X,
  input  Y,
  input  L_i,
  input  OS,
  output L_o,
  output D___X_Y
);

  wire and_1_out, and_2_out, not_1_out, sub1bit_1_d;

  Sub1bit sub1bit_1 (.A(X), .B(Y), .L_0___A___B(L_o), .L_i(L_i), .D(sub1bit_1_d));
  not not_1 (not_1_out, OS);
  and and_1 (and_1_out, sub1bit_1_d, not_1_out);
  and and_2 (and_2_out, X, OS);
  or or_1 (D___X_Y, and_1_out, and_2_out);
endmodule

module Sub1bit (
  input  A,
  input  B,
  input  L_i,
  output L_0___A___B,
  output D
);

  wire and_1_out, and_2_out, not_1_out, not_2_out, xor_1_out;

  or or_1 (L_0___A___B, and_1_out, and_2_out);
  not not_1 (not_1_out, A);
  and and_1 (and_1_out, not_1_out, B);
  not not_2 (not_2_out, xor_1_out);
  and and_2 (and_2_out, not_2_out, L_i);
  xor xor_1 (xor_1_out, B, A);
  xor xor_2 (D, L_i, xor_1_out);
endmodule

module _2bitdiv (
  input  [1:0] B,
  input  [1:0] A,
  output [1:0] A_B,
  output [1:0] A_B_2
);

  wire divblock_1_l_o, divblock_2_d___x_y, divblock_2_l_o, divblock_3_l_o, divblock_4_l_o;

  not not_1 (A_B[1], divblock_1_l_o);
  DivBlock divblock_1 (
    .Y(B[1]), .X(1'b0), .L_o(divblock_1_l_o), .OS(divblock_1_l_o), .L_i(divblock_2_l_o));  // open: D___X_Y
  not not_2 (A_B[0], divblock_3_l_o);
  DivBlock divblock_2 (
    .Y(B[0]), .X(A[1]), .L_o(divblock_2_l_o), .OS(divblock_1_l_o), .D___X_Y(divblock_2_d___x_y), .L_i(1'b0));
  DivBlock divblock_3 (
    .Y(B[1]), .X(divblock_2_d___x_y), .L_o(divblock_3_l_o), .OS(divblock_3_l_o), .D___X_Y(A_B_2[1]),
    .L_i(divblock_4_l_o));
  DivBlock divblock_4 (.Y(B[0]), .X(A[0]), .L_o(divblock_4_l_o), .OS(divblock_3_l_o), .D___X_Y(A_B_2[0]), .L_i(1'b0));
endmodule
