// Logisim project SomaBit.circ as structural Verilog: 11 circuits, main circuit main
module main (
  input  [7:0] in_1,
  input  [7:0] in_2,
  output [7:0] out_3,
  output Overflow
);

  wire soma_1_carry_out, soma_2_carry_out, soma_3_carry_out, soma_4_carry_out, soma_5_carry_out,
       soma_6_carry_out, soma_7_carry_out;

  Soma soma_1 (.Bit1(in_1[0]), .Bit2(in_2[0]), .Carry_Out(soma_1_carry_out), .Out(out_3[0]));  // open: Carry_In
  Soma soma_2 (
    .Bit1(in_1[1]), .Bit2(in_2[1]), .Carry_In(soma_1_carry_out), .Carry_Out(soma_2_carry_out), .Out(out_3[1]));
  Soma soma_3 (
    .Bit1(in_1[2]), .Bit2(in_2[2]), .Carry_In(soma_2_carry_out), .Carry_Out(soma_3_carry_out), .Out(out_3[2]));
  Soma soma_4 (
    .Bit1(in_1[3]), .Bit2(in_2[3]), .Carry_In(soma_3_carry_out), .Carry_Out(soma_4_carry_out), .Out(out_3[3]));
  Soma soma_5 (
    .Bit1(in_1[4]), .Bit2(in_2[4]), .Carry_In(soma_4_carry_out), .Carry_Out(soma_5_carry_out), .Out(out_3[4]));
  Soma soma_6 (
    .Bit1(in_1[5]), .Bit2(in_2[5]), .Carry_In(soma_5_carry_out), .Carry_Out(soma_6_carry_out), .Out(out_3[5]));
  Soma soma_7 (
    .Bit1(in_1[6]), .Bit2(in_2[6]), .Carry_In(soma_6_carry_out), .Carry_Out(soma_7_carry_out), .Out(out_3[6]));
  Soma soma_8 (.Bit1(in_1[7]), .Bit2(in_2[7]), .Carry_In(soma_7_carry_out), .Carry_Out(Overflow), .Out(out_3[7]));
endmodule

module Soma (
  input  Carry_In,
  input  Bit1,
  input  Bit2,
  output Out,
  output Carry_Out
);

  wire and_1_out, and_2_out, xor_1_out;

  and and_1 (and_1_out, Bit1, Bit2);
  xor xor_1 (xor_1_out, Bit1, Bit2);
  or or_1 (Carry_Out, and_1_out, and_2_out);
  and and_2 (and_2_out, xor_1_out, Carry_In);
  xor xor_2 (Out, Carry_In, xor_1_out);
endmodule

module Inversor (
  input  [7:0] in_1,
  output [7:0] out_2
);

  not not_1 (out_2[0], in_1[0]);
  not not_2 (out_2[1], in_1[1]);
  not not_3 (out_2[2], in_1[2]);
  not not_4 (out_2[3], in_1[3]);
  not not_5 (out_2[4], in_1[4]);
  not not_6 (out_2[5], in_1[5]);
  not not_7 (out_2[6], in_1[6]);
  not not_8 (out_2[7], in_1[7]);
endmodule

module Soma_8bits (
  input  [7:0] Num1,
  input  [7:0] Num2,
  output [7:0] Result,
  output Overflow
);

  wire soma_1_carry_out, soma_2_carry_out, soma_3_carry_out, soma_4_carry_out, soma_5_carry_out,
       soma_6_carry_out, soma_7_carry_out;

  Soma soma_1 (.Bit1(Num1[0]), .Bit2(Num2[0]), .Carry_Out(soma_1_carry_out), .Out(Result[0]));  // open: Carry_In
  Soma soma_2 (
    .Bit1(Num1[1]), .Bit2(Num2[1]), .Carry_In(soma_1_carry_out), .Carry_Out(soma_2_carry_out), .Out(Result[1]));
  Soma soma_3 (
    .Bit1(Num1[2]), .Bit2(Num2[2]), .Carry_In(soma_2_carry_out), .Carry_Out(soma_3_carry_out), .Out(Result[2]));
  Soma soma_4 (
    .Bit1(Num1[3]), .Bit2(Num2[3]), .Carry_In(soma_3_carry_out), .Carry_Out(soma_4_carry_out), .Out(Result[3]));
  Soma soma_5 (
    .Bit1(Num1[4]), .Bit2(Num2[4]), .Carry_In(soma_4_carry_out), .Carry_Out(soma_5_carry_out), .Out(Result[4]));
  Soma soma_6 (
    .Bit1(Num1[5]), .Bit2(Num2[5]), .Carry_In(soma_5_carry_out), .Carry_Out(soma_6_carry_out), .Out(Result[5]));
  Soma soma_7 (
    .Bit1(Num1[6]), .Bit2(Num2[6]), .Carry_In(soma_6_carry_out), .Carry_Out(soma_7_carry_out), .Out(Result[6]));
  Soma soma_8 (.Bit1(Num1[7]), .Bit2(Num2[7]), .Carry_In(soma_7_carry_out), .Carry_Out(Overflow), .Out(Result[7]));
endmodule

module Subtrai_8bits (
  input  [7:0] Num1,
  input  [7:0] Num2,
  output [7:0] out_3,
  output Overflow
);

  wire and_1_out, and_2_out, not_1_out, not_2_out, not_3_out;
  wire [7:0] signchange_1_out;

  SignChange signchange_1 (.Num(Num2), .out(signchange_1_out));
  Soma_8bits soma_8bits_1 (.Num1(Num1), .Num2(signchange_1_out), .Result(out_3));  // open: Overflow
  not not_1 (not_1_out, out_3[7]);
  not not_2 (not_2_out, signchange_1_out[7]);
  not not_3 (not_3_out, signchange_1_out[7]);
  and and_1 (and_1_out, signchange_1_out[7], not_1_out, Num1[7]);
  and and_2 (and_2_out, not_2_out, out_3[7], not_3_out);
  or or_1 (Overflow, and_1_out, and_2_out);
endmodule

module Multiplica (
  input  [7:0] Num1,
  input  [7:0] Num2,
  output [7:0] Out,
  output out_4
);

  wire and_1_out, and_2_out, and_3_out, and_4_out, not_1_out, not_2_out, not_3_out, not_4_out, not_5_out,
       not_6_out, or_1_out, or_2_out, or_3_out, or_4_out, or_5_out, or_7_out, or_8_out, or_9_out,
       shiftleft_1_ovfl, shiftleft_2_ovfl, shiftleft_3_ovfl, shiftleft_4_ovfl, shiftleft_5_ovfl,
       shiftleft_6_ovfl, shiftleft_7_ovfl, shiftleft_8_ovfl, shiftleft_9_ovfl, shiftleft_10_ovfl,
       shiftleft_11_ovfl, shiftleft_12_ovfl, shiftleft_13_ovfl, shiftleft_14_ovfl, shiftleft_15_ovfl,
       shiftleft_16_ovfl, shiftleft_17_ovfl, shiftleft_18_ovfl, shiftleft_19_ovfl, shiftleft_20_ovfl,
       shiftleft_21_ovfl, shiftleft_22_ovfl, shiftleft_23_ovfl, shiftleft_24_ovfl, shiftleft_25_ovfl,
       shiftleft_26_ovfl, shiftleft_27_ovfl, shiftleft_28_ovfl, soma_8bits_1_overflow, soma_8bits_2_overflow,
       soma_8bits_3_overflow, soma_8bits_4_overflow, soma_8bits_5_overflow, soma_8bits_6_overflow,
       soma_8bits_7_overflow, xor_1_out;
  wire [7:0] filtro_1_out, filtro_2_out, filtro_3_out, filtro_4_out, filtro_5_out, filtro_6_out,
       filtro_7_out, filtro_8_out, inversorcond_1_out, inversorcond_2_out, shiftleft_1_out, shiftleft_2_out,
       shiftleft_3_out, shiftleft_4_out, shiftleft_5_out, shiftleft_6_out, shiftleft_7_out, shiftleft_8_out,
       shiftleft_9_out, shiftleft_10_out, shiftleft_11_out, shiftleft_12_out, shiftleft_13_out,
       shiftleft_14_out, shiftleft_15_out, shiftleft_16_out, shiftleft_17_out, shiftleft_18_out,
       shiftleft_19_out, shiftleft_20_out, shiftleft_21_out, shiftleft_22_out, shiftleft_23_out,
       shiftleft_24_out, shiftleft_25_out, shiftleft_26_out, shiftleft_27_out, shiftleft_28_out,
       soma_8bits_1_result, soma_8bits_2_result, soma_8bits_3_result, soma_8bits_4_result,
       soma_8bits_5_result, soma_8bits_6_result, soma_8bits_7_result;

  InversorCond inversorcond_1 (.Num(Num1), .Ctrl(Num1[7]), .Out(inversorcond_1_out));
  InversorCond inversorcond_2 (.Num(Num2), .Ctrl(Num2[7]), .Out(inversorcond_2_out));
  not not_1 (not_1_out, Num1[7]);
  not not_2 (not_2_out, Num2[7]);
  not not_3 (not_3_out, Num1[7]);
  not not_4 (not_4_out, Out[7]);
  not not_5 (not_5_out, Out[7]);
  not not_6 (not_6_out, Num2[7]);
  Filtro filtro_1 (.In(inversorcond_1_out), .Crtl(inversorcond_2_out[0]), .Out(filtro_1_out));
  Filtro filtro_2 (.In(inversorcond_1_out), .Crtl(inversorcond_2_out[1]), .Out(filtro_2_out));
  Filtro filtro_3 (.In(inversorcond_1_out), .Crtl(inversorcond_2_out[2]), .Out(filtro_3_out));
  Filtro filtro_4 (.In(inversorcond_1_out), .Crtl(inversorcond_2_out[3]), .Out(filtro_4_out));
  Filtro filtro_5 (.In(inversorcond_1_out), .Crtl(inversorcond_2_out[4]), .Out(filtro_5_out));
  Filtro filtro_6 (.In(inversorcond_1_out), .Crtl(inversorcond_2_out[5]), .Out(filtro_6_out));
  Filtro filtro_7 (.In(inversorcond_1_out), .Crtl(inversorcond_2_out[6]), .Out(filtro_7_out));
  Filtro filtro_8 (.In(inversorcond_1_out), .Crtl(inversorcond_2_out[7]), .Out(filtro_8_out));
  and and_1 (and_1_out, not_1_out, Out[7], not_2_out);
  and and_2 (and_2_out, Num1[7], Out[7], Num2[7]);
  and and_3 (and_3_out, not_3_out, not_4_out, Num2[7]);
  and and_4 (and_4_out, Num1[7], not_5_out, not_6_out);
  ShiftLeft shiftleft_1 (.In(filtro_2_out), .Out(shiftleft_1_out), .Ovfl(shiftleft_1_ovfl));
  ShiftLeft shiftleft_2 (.In(filtro_3_out), .Out(shiftleft_2_out), .Ovfl(shiftleft_2_ovfl));
  ShiftLeft shiftleft_3 (.In(filtro_4_out), .Out(shiftleft_3_out), .Ovfl(shiftleft_3_ovfl));
  ShiftLeft shiftleft_4 (.In(filtro_5_out), .Out(shiftleft_4_out), .Ovfl(shiftleft_4_ovfl));
  ShiftLeft shiftleft_5 (.In(filtro_6_out), .Out(shiftleft_5_out), .Ovfl(shiftleft_5_ovfl));
  ShiftLeft shiftleft_6 (.In(filtro_7_out), .Out(shiftleft_6_out), .Ovfl(shiftleft_6_ovfl));
  ShiftLeft shiftleft_7 (.In(filtro_8_out), .Out(shiftleft_7_out), .Ovfl(shiftleft_7_ovfl));
  or or_1 (or_1_out, shiftleft_7_ovfl, shiftleft_6_ovfl, shiftleft_5_ovfl, shiftleft_4_ovfl, shiftleft_3_ovfl, shiftleft_2_ovfl, shiftleft_1_ovfl);
  ShiftLeft shiftleft_8 (.In(shiftleft_2_out), .Out(shiftleft_8_out), .Ovfl(shiftleft_8_ovfl));
  ShiftLeft shiftleft_9 (.In(shiftleft_3_out), .Out(shiftleft_9_out), .Ovfl(shiftleft_9_ovfl));
  ShiftLeft shiftleft_10 (.In(shiftleft_4_out), .Out(shiftleft_10_out), .Ovfl(shiftleft_10_ovfl));
  ShiftLeft shiftleft_11 (.In(shiftleft_5_out), .Out(shiftleft_11_out), .Ovfl(shiftleft_11_ovfl));
  ShiftLeft shiftleft_12 (.In(shiftleft_6_out), .Out(shiftleft_12_out), .Ovfl(shiftleft_12_ovfl));
  ShiftLeft shiftleft_13 (.In(shiftleft_7_out), .Out(shiftleft_13_out), .Ovfl(shiftleft_13_ovfl));
  or or_2 (or_2_out, and_1_out, and_2_out, and_3_out, and_4_out);
  or or_3 (or_3_out, shiftleft_13_ovfl, shiftleft_12_ovfl, shiftleft_11_ovfl, shiftleft_10_ovfl, shiftleft_9_ovfl, shiftleft_8_ovfl);
  ShiftLeft shiftleft_14 (.In(shiftleft_9_out), .Out(shiftleft_14_out), .Ovfl(shiftleft_14_ovfl));
  ShiftLeft shiftleft_15 (.In(shiftleft_10_out), .Out(shiftleft_15_out), .Ovfl(shiftleft_15_ovfl));
  ShiftLeft shiftleft_16 (.In(shiftleft_11_out), .Out(shiftleft_16_out), .Ovfl(shiftleft_16_ovfl));
  ShiftLeft shiftleft_17 (.In(shiftleft_12_out), .Out(shiftleft_17_out), .Ovfl(shiftleft_17_ovfl));
  ShiftLeft shiftleft_18 (.In(shiftleft_13_out), .Out(shiftleft_18_out), .Ovfl(shiftleft_18_ovfl));
  or or_4 (or_4_out, shiftleft_18_ovfl, shiftleft_17_ovfl, shiftleft_16_ovfl, shiftleft_15_ovfl, shiftleft_14_ovfl);
  ShiftLeft shiftleft_19 (.In(shiftleft_15_out), .Out(shiftleft_19_out), .Ovfl(shiftleft_19_ovfl));
  ShiftLeft shiftleft_20 (.In(shiftleft_16_out), .Out(shiftleft_20_out), .Ovfl(shiftleft_20_ovfl));
  ShiftLeft shiftleft_21 (.In(shiftleft_17_out), .Out(shiftleft_21_out), .Ovfl(shiftleft_21_ovfl));
  ShiftLeft shiftleft_22 (.In(shiftleft_18_out), .Out(shiftleft_22_out), .Ovfl(shiftleft_22_ovfl));
  or or_5 (or_5_out, shiftleft_22_ovfl, shiftleft_21_ovfl, shiftleft_20_ovfl, shiftleft_19_ovfl);
  or or_6 (out_4, or_2_out, or_1_out, or_3_out, or_4_out, or_5_out, or_7_out, or_8_out, shiftleft_27_ovfl, or_9_out);
  ShiftLeft shiftleft_23 (.In(shiftleft_20_out), .Out(shiftleft_23_out), .Ovfl(shiftleft_23_ovfl));
  ShiftLeft shiftleft_24 (.In(shiftleft_21_out), .Out(shiftleft_24_out), .Ovfl(shiftleft_24_ovfl));
  ShiftLeft shiftleft_25 (.In(shiftleft_22_out), .Out(shiftleft_25_out), .Ovfl(shiftleft_25_ovfl));
  or or_7 (or_7_out, shiftleft_25_ovfl, shiftleft_24_ovfl, shiftleft_23_ovfl);
  ShiftLeft shiftleft_26 (.In(shiftleft_24_out), .Out(shiftleft_26_out), .Ovfl(shiftleft_26_ovfl));
  ShiftLeft shiftleft_27 (.In(shiftleft_28_out), .Out(shiftleft_27_out), .Ovfl(shiftleft_27_ovfl));
  ShiftLeft shiftleft_28 (.In(shiftleft_25_out), .Out(shiftleft_28_out), .Ovfl(shiftleft_28_ovfl));
  or or_8 (or_8_out, shiftleft_28_ovfl, shiftleft_26_ovfl);
  Soma_8bits soma_8bits_1 (
    .Num1(filtro_1_out), .Num2(shiftleft_1_out), .Result(soma_8bits_1_result),
    .Overflow(soma_8bits_1_overflow));
  Soma_8bits soma_8bits_2 (
    .Num1(soma_8bits_1_result), .Num2(shiftleft_8_out), .Result(soma_8bits_2_result),
    .Overflow(soma_8bits_2_overflow));
  Soma_8bits soma_8bits_3 (
    .Num1(soma_8bits_2_result), .Num2(shiftleft_14_out), .Result(soma_8bits_3_result),
    .Overflow(soma_8bits_3_overflow));
  Soma_8bits soma_8bits_4 (
    .Num1(soma_8bits_3_result), .Num2(shiftleft_19_out), .Result(soma_8bits_4_result),
    .Overflow(soma_8bits_4_overflow));
  Soma_8bits soma_8bits_5 (
    .Num1(soma_8bits_4_result), .Num2(shiftleft_23_out), .Result(soma_8bits_5_result),
    .Overflow(soma_8bits_5_overflow));
  Soma_8bits soma_8bits_6 (
    .Num1(soma_8bits_5_result), .Num2(shiftleft_26_out), .Result(soma_8bits_6_result),
    .Overflow(soma_8bits_6_overflow));
  Soma_8bits soma_8bits_7 (
    .Num1(soma_8bits_6_result), .Num2(shiftleft_27_out), .Result(soma_8bits_7_result),
    .Overflow(soma_8bits_7_overflow));
  xor xor_1 (xor_1_out, Num1[7], Num2[7]);
  InversorCond inversorcond_3 (.Num(soma_8bits_7_result), .Ctrl(xor_1_out), .Out(Out));
  or or_9 (or_9_out, soma_8bits_7_overflow, soma_8bits_6_overflow, soma_8bits_5_overflow, soma_8bits_4_overflow, soma_8bits_3_overflow, soma_8bits_2_overflow, soma_8bits_1_overflow);
endmodule

module ShiftLeft (
  input  [7:0] In,
  output [7:0] Out,
  output Ovfl
);

  wire and_1_out, and_3_out, and_4_out, and_5_out, and_6_out, and_7_out, and_8_out, and_9_out, and_10_out,
       and_11_out, and_12_out, and_14_out, not_1_out;

  not not_1 (not_1_out, 1'b1);
  and and_1 (and_1_out, In[0], 1'b1);
  and and_2 (Out[0], not_1_out, In[1]);
  and and_3 (and_3_out, In[1], 1'b1);
  or or_1 (Out[1], and_1_out, and_4_out);
  and and_4 (and_4_out, not_1_out, In[2]);
  or or_2 (Out[2], and_3_out, and_5_out);
  and and_5 (and_5_out, not_1_out, In[3]);
  and and_6 (and_6_out, In[2], 1'b1);
  and and_7 (and_7_out, In[3], 1'b1);
  or or_3 (Out[3], and_6_out, and_8_out);
  and and_8 (and_8_out, not_1_out, In[4]);
  and and_9 (and_9_out, In[4], 1'b1);
  or or_4 (Out[4], and_7_out, and_11_out);
  and and_10 (and_10_out, In[5], 1'b1);
  and and_11 (and_11_out, not_1_out, In[5]);
  or or_5 (Out[5], and_9_out, and_12_out);
  and and_12 (and_12_out, not_1_out, In[6]);
  and and_13 (Out[7], In[6], 1'b1);
  or or_6 (Out[6], and_10_out, and_14_out);
  and and_14 (and_14_out, not_1_out, In[7]);

  assign Ovfl = In[7];
endmodule

module Filtro (
  input  [7:0] In,
  input  Crtl,
  output [7:0] Out
);

  and and_1 (Out[0], In[0], Crtl);
  and and_2 (Out[1], In[1], Crtl);
  and and_3 (Out[2], In[2], Crtl);
  and and_4 (Out[3], In[3], Crtl);
  and and_5 (Out[4], In[4], Crtl);
  and and_6 (Out[5], In[5], Crtl);
  and and_7 (Out[6], In[6], Crtl);
  and and_8 (Out[7], In[7], Crtl);
endmodule

module SignChange (
  input  [7:0] Num,
  output [7:0] out
);

  wire [7:0] inversor_1_out_2;

  Inversor inversor_1 (.in_1(Num), .out_2(inversor_1_out_2));
  Soma_8bits soma_8bits_1 (.Num1(8'h1), .Num2(inversor_1_out_2), .Result(out));  // open: Overflow
endmodule

module InversorCond (
  input  Ctrl,
  input  [7:0] Num,
  output [7:0] Out
);

  wire and_1_out, and_2_out, and_3_out, and_4_out, and_5_out, and_6_out, and_7_out, and_8_out, and_9_out,
       and_10_out, and_11_out, and_12_out, and_13_out, and_14_out, and_15_out, and_16_out, not_1_out,
       not_2_out, not_3_out, not_4_out, not_5_out, not_6_out, not_7_out, not_8_out, not_9_out;
  wire [7:0] signchange_1_out;

  SignChange signchange_1 (.Num(Num), .out(signchange_1_out));
  not not_1 (not_1_out, Ctrl);
  and and_1 (and_1_out, Num[0], not_1_out);
  and and_2 (and_2_out, Num[1], not_1_out);
  and and_3 (and_3_out, Num[2], not_1_out);
  and and_4 (and_4_out, Num[3], not_1_out);
  and and_5 (and_5_out, Num[4], not_1_out);
  and and_6 (and_6_out, Num[5], not_1_out);
  and and_7 (and_7_out, Num[6], not_1_out);
  and and_8 (and_8_out, Num[7], not_1_out);
  and and_9 (and_9_out, signchange_1_out[0], not_2_out);
  not not_2 (not_2_out, not_1_out);
  and and_10 (and_10_out, signchange_1_out[1], not_3_out);
  not not_3 (not_3_out, not_1_out);
  and and_11 (and_11_out, signchange_1_out[2], not_4_out);
  not not_4 (not_4_out, not_1_out);
  and and_12 (and_12_out, signchange_1_out[3], not_5_out);
  not not_5 (not_5_out, not_1_out);
  and and_13 (and_13_out, signchange_1_out[4], not_6_out);
  not not_6 (not_6_out, not_1_out);
  and and_14 (and_14_out, signchange_1_out[5], not_7_out);
  not not_7 (not_7_out, not_1_out);
  and and_15 (and_15_out, signchange_1_out[6], not_8_out);
  not not_8 (not_8_out, not_1_out);
  and and_16 (and_16_out, signchange_1_out[7], not_9_out);
  not not_9 (not_9_out, not_1_out);
  or or_1 (Out[0], and_1_out, and_9_out);
  or or_2 (Out[1], and_2_out, and_10_out);
  or or_3 (Out[2], and_3_out, and_11_out);
  or or_4 (Out[3], and_4_out, and_12_out);
  or or_5 (Out[4], and_5_out, and_13_out);
  or or_6 (Out[5], and_6_out, and_14_out);
  or or_7 (Out[6], and_7_out, and_15_out);
  or or_8 (Out[7], and_8_out, and_16_out);
endmodule

module Multiplica2 (
  input  [7:0] In,
  input  [7:0] In_2,
  output [7:0] out_3
);

  wire and_1_out, and_2_out, and_3_out, and_4_out, and_5_out, and_6_out, and_7_out, and_8_out, and_9_out,
       and_10_out, and_11_out, and_12_out, and_13_out, and_14_out, and_15_out, and_16_out, and_17_out,
       and_18_out, and_19_out, and_20_out, and_21_out, and_22_out, and_23_out, and_24_out, and_25_out,
       and_26_out, and_27_out, and_28_out, and_29_out, and_30_out, and_31_out, and_32_out, and_33_out,
       and_34_out, and_35_out, soma_1_carry_out, soma_1_out, soma_2_carry_out, soma_2_out, soma_3_carry_out,
       soma_3_out, soma_4_carry_out, soma_4_out, soma_5_carry_out, soma_5_out, soma_6_carry_out, soma_6_out,
       soma_7_carry_out, soma_8_carry_out, soma_8_out, soma_9_carry_out, soma_9_out, soma_10_carry_out,
       soma_10_out, soma_11_carry_out, soma_11_out, soma_12_carry_out, soma_12_out, soma_13_carry_out,
       soma_14_carry_out, soma_14_out, soma_15_carry_out, soma_15_out, soma_16_carry_out, soma_16_out,
       soma_17_carry_out, soma_17_out, soma_18_carry_out, soma_19_carry_out, soma_19_out, soma_20_carry_out,
       soma_20_out, soma_21_carry_out, soma_21_out, soma_22_carry_out, soma_23_carry_out, soma_23_out,
       soma_24_carry_out, soma_24_out, soma_25_carry_out, soma_26_carry_out, soma_26_out, soma_27_carry_out,
       soma_28_carry_out;

  InversorCond inversorcond_1 ();  // open: Num, Ctrl, Out
  and and_1 (and_1_out, In[7], In_2[0]);
  and and_2 (and_2_out, In[6], In_2[1]);
  Soma soma_1 (
    .Bit1(and_2_out), .Bit2(and_1_out), .Carry_In(soma_8_carry_out), .Carry_Out(soma_1_carry_out),
    .Out(soma_1_out));
  and and_3 (and_3_out, In[5], In_2[2]);
  Soma soma_2 (
    .Bit1(and_3_out), .Bit2(soma_1_out), .Carry_In(soma_9_carry_out), .Carry_Out(soma_2_carry_out),
    .Out(soma_2_out));
  and and_4 (and_4_out, In[4], In_2[3]);
  Soma soma_3 (
    .Bit1(and_4_out), .Bit2(soma_2_out), .Carry_In(soma_10_carry_out), .Carry_Out(soma_3_carry_out),
    .Out(soma_3_out));
  and and_5 (and_5_out, In[3], In_2[4]);
  Soma soma_4 (
    .Bit1(and_5_out), .Bit2(soma_3_out), .Carry_In(soma_11_carry_out), .Carry_Out(soma_4_carry_out),
    .Out(soma_4_out));
  and and_6 (and_6_out, In[2], In_2[5]);
  Soma soma_5 (
    .Bit1(and_6_out), .Bit2(soma_4_out), .Carry_In(soma_12_carry_out), .Carry_Out(soma_5_carry_out),
    .Out(soma_5_out));
  and and_7 (and_7_out, In[1], In_2[6]);
  Soma soma_6 (
    .Bit1(and_7_out), .Bit2(soma_5_out), .Carry_In(soma_13_carry_out), .Carry_Out(soma_6_carry_out),
    .Out(soma_6_out));
  and and_8 (and_8_out, In[0], In_2[7]);
  Soma soma_7 (.Bit1(and_8_out), .Bit2(soma_6_out), .Carry_In(1'b0), .Carry_Out(soma_7_carry_out), .Out(out_3[7]));
  and and_9 (and_9_out, In[6], In_2[0]);
  and and_10 (and_10_out, In[5], In_2[1]);
  Soma soma_8 (
    .Bit1(and_10_out), .Bit2(and_9_out), .Carry_In(soma_14_carry_out), .Carry_Out(soma_8_carry_out),
    .Out(soma_8_out));
  and and_11 (and_11_out, In[4], In_2[2]);
  Soma soma_9 (
    .Bit1(and_11_out), .Bit2(soma_8_out), .Carry_In(soma_15_carry_out), .Carry_Out(soma_9_carry_out),
    .Out(soma_9_out));
  and and_12 (and_12_out, In[3], In_2[3]);
  Soma soma_10 (
    .Bit1(and_12_out), .Bit2(soma_9_out), .Carry_In(soma_16_carry_out), .Carry_Out(soma_10_carry_out),
    .Out(soma_10_out));
  and and_13 (and_13_out, In[2], In_2[4]);
  Soma soma_11 (
    .Bit1(and_13_out), .Bit2(soma_10_out), .Carry_In(soma_17_carry_out), .Carry_Out(soma_11_carry_out),
    .Out(soma_11_out));
  and and_14 (and_14_out, In[1], In_2[5]);
  Soma soma_12 (
    .Bit1(and_14_out), .Bit2(soma_11_out), .Carry_In(soma_18_carry_out), .Carry_Out(soma_12_carry_out),
    .Out(soma_12_out));
  and and_15 (and_15_out, In[0], In_2[6]);
  Soma soma_13 (.Bit1(and_15_out), .Bit2(soma_12_out), .Carry_In(1'b0), .Carry_Out(soma_13_carry_out), .Out(out_3[6]));
  and and_16 (and_16_out, In[5], In_2[0]);
  and and_17 (and_17_out, In[4], In_2[1]);
  Soma soma_14 (
    .Bit1(and_17_out), .Bit2(and_16_out), .Carry_In(soma_19_carry_out), .Carry_Out(soma_14_carry_out),
    .Out(soma_14_out));
  and and_18 (and_18_out, In[3], In_2[2]);
  Soma soma_15 (
    .Bit1(and_18_out), .Bit2(soma_14_out), .Carry_In(soma_20_carry_out), .Carry_Out(soma_15_carry_out),
    .Out(soma_15_out));
  and and_19 (and_19_out, In[2], In_2[3]);
  Soma soma_16 (
    .Bit1(and_19_out), .Bit2(soma_15_out), .Carry_In(soma_21_carry_out), .Carry_Out(soma_16_carry_out),
    .Out(soma_16_out));
  and and_20 (and_20_out, In[1], In_2[4]);
  Soma soma_17 (
    .Bit1(and_20_out), .Bit2(soma_16_out), .Carry_In(soma_22_carry_out), .Carry_Out(soma_17_carry_out),
    .Out(soma_17_out));
  and and_21 (and_21_out, In[0], In_2[5]);
  Soma soma_18 (.Bit1(and_21_out), .Bit2(soma_17_out), .Carry_In(1'b0), .Carry_Out(soma_18_carry_out), .Out(out_3[5]));
  and and_22 (and_22_out, In[4], In_2[0]);
  and and_23 (and_23_out, In[3], In_2[1]);
  Soma soma_19 (
    .Bit1(and_23_out), .Bit2(and_22_out), .Carry_In(soma_23_carry_out), .Carry_Out(soma_19_carry_out),
    .Out(soma_19_out));
  and and_24 (and_24_out, In[2], In_2[2]);
  Soma soma_20 (
    .Bit1(and_24_out), .Bit2(soma_19_out), .Carry_In(soma_26_carry_out), .Carry_Out(soma_20_carry_out),
    .Out(soma_20_out));
  and and_25 (and_25_out, In[1], In_2[3]);
  Soma soma_21 (
    .Bit1(and_25_out), .Bit2(soma_20_out), .Carry_In(soma_27_carry_out), .Carry_Out(soma_21_carry_out),
    .Out(soma_21_out));
  and and_26 (and_26_out, In[0], In_2[4]);
  Soma soma_22 (.Bit1(and_26_out), .Bit2(soma_21_out), .Carry_In(1'b0), .Carry_Out(soma_22_carry_out), .Out(out_3[4]));
  and and_27 (and_27_out, In[3], In_2[0]);
  and and_28 (and_28_out, In[2], In_2[0]);
  and and_29 (and_29_out, In[1], In_2[1]);
  and and_30 (and_30_out, In[2], In_2[1]);
  Soma soma_23 (
    .Bit1(and_30_out), .Bit2(and_27_out), .Carry_In(soma_24_carry_out), .Carry_Out(soma_23_carry_out),
    .Out(soma_23_out));
  Soma soma_24 (
    .Bit1(and_29_out), .Bit2(and_28_out), .Carry_In(soma_28_carry_out), .Carry_Out(soma_24_carry_out),
    .Out(soma_24_out));
  and and_31 (and_31_out, In[1], In_2[2]);
  and and_32 (and_32_out, In[0], In_2[2]);
  Soma soma_25 (.Bit1(and_32_out), .Bit2(soma_24_out), .Carry_In(1'b0), .Carry_Out(soma_25_carry_out), .Out(out_3[2]));
  Soma soma_26 (
    .Bit1(and_31_out), .Bit2(soma_23_out), .Carry_In(soma_25_carry_out), .Carry_Out(soma_26_carry_out),
    .Out(soma_26_out));
  and and_33 (and_33_out, In[0], In_2[3]);
  Soma soma_27 (.Bit1(and_33_out), .Bit2(soma_26_out), .Carry_In(1'b0), .Carry_Out(soma_27_carry_out), .Out(out_3[3]));
  and and_34 (and_34_out, In[1], In_2[0]);
  and and_35 (and_35_out, In[0], In_2[1]);
  Soma soma_28 (.Bit1(and_35_out), .Bit2(and_34_out), .Carry_In(1'b0), .Carry_Out(soma_28_carry_out), .Out(out_3[1]));
  and and_36 (out_3[0], In[0], In_2[0]);
endmodule
