// Logisim project SomaLib.circ as structural Verilog: 8 circuits, main circuit Soma1bit
module Soma1bit (
  input  Carry_In,
  input  Bit1,
  input  Bit2,
  output Out,
  output Carry_Out
);

  wire and_1_out, and_2_out, xor_1_out;

  and and_1 (and_1_out, Bit1, Bit2);
  xor xor_1 (xor_1_out, Bit1, Bit2);
  or or_1 (Carry_Out, and_1_out, and_2_out);
  and and_2 (and_2_out, xor_1_out, Carry_In);
  xor xor_2 (Out, Carry_In, xor_1_out);
endmodule

module Inversor (
  input  [7:0] in_1,
  output [7:0] out_2
);

  not not_1 (out_2[0], in_1[0]);
  not not_2 (out_2[1], in_1[1]);
  not not_3 (out_2[2], in_1[2]);
  not not_4 (out_2[3], in_1[3]);
  not not_5 (out_2[4], in_1[4]);
  not not_6 (out_2[5], in_1[5]);
  not not_7 (out_2[6], in_1[6]);
  not not_8 (out_2[7], in_1[7]);
endmodule

module Soma8bits (
  input  [7:0] Num1,
  input  [7:0] Num2,
  output [7:0] Result,
  output Overflow
);

  wire and_1_out, and_2_out, not_1_out, not_2_out, not_3_out, soma1bit_1_carry_out, soma1bit_2_carry_out,
       soma1bit_3_carry_out, soma1bit_4_carry_out, soma1bit_5_carry_out, soma1bit_6_carry_out,
       soma1bit_7_carry_out;

  Soma1bit soma1bit_1 (
    .Bit1(Num1[0]), .Bit2(Num2[0]), .Out(Result[0]), .Carry_In(1'b0), .Carry_Out(soma1bit_1_carry_out));
  Soma1bit soma1bit_2 (
    .Bit1(Num1[1]), .Bit2(Num2[1]), .Out(Result[1]), .Carry_In(soma1bit_1_carry_out),
    .Carry_Out(soma1bit_2_carry_out));
  Soma1bit soma1bit_3 (
    .Bit1(Num1[2]), .Bit2(Num2[2]), .Out(Result[2]), .Carry_In(soma1bit_2_carry_out),
    .Carry_Out(soma1bit_3_carry_out));
  Soma1bit soma1bit_4 (
    .Bit1(Num1[3]), .Bit2(Num2[3]), .Out(Result[3]), .Carry_In(soma1bit_3_carry_out),
    .Carry_Out(soma1bit_4_carry_out));
  Soma1bit soma1bit_5 (
    .Bit1(Num1[4]), .Bit2(Num2[4]), .Out(Result[4]), .Carry_In(soma1bit_4_carry_out),
    .Carry_Out(soma1bit_5_carry_out));
  Soma1bit soma1bit_6 (
    .Bit1(Num1[5]), .Bit2(Num2[5]), .Out(Result[5]), .Carry_In(soma1bit_5_carry_out),
    .Carry_Out(soma1bit_6_carry_out));
  Soma1bit soma1bit_7 (
    .Bit1(Num1[6]), .Bit2(Num2[6]), .Out(Result[6]), .Carry_In(soma1bit_6_carry_out),
    .Carry_Out(soma1bit_7_carry_out));
  Soma1bit soma1bit_8 (
    .Bit1(Num1[7]), .Bit2(Num2[7]), .Out(Result[7]), .Carry_In(soma1bit_7_carry_out));  // open: Carry_Out
  not not_1 (not_1_out, Num1[7]);
  and and_1 (and_1_out, not_1_out, Result[7], not_2_out);
  not not_2 (not_2_out, Num2[7]);
  not not_3 (not_3_out, Result[7]);
  and and_2 (and_2_out, Num1[7], not_3_out, Num2[7]);
  or or_1 (Overflow, and_1_out, and_2_out);
endmodule

module Subtrai_8bits (
  input  [7:0] Num1,
  input  [7:0] Num2,
  output [7:0] Out,
  output Overflow
);

  wire [7:0] signchange_1_out;

  SignChange signchange_1 (.Num(Num2), .out(signchange_1_out));
  Soma8bits soma8bits_1 (.Num1(Num1), .Num2(signchange_1_out), .Result(Out), .Overflow(Overflow));
endmodule

module ShiftLeft (
  input  [7:0] In,
  output [7:0] Out,
  output Ovfl
);

  wire and_1_out, and_3_out, and_4_out, and_5_out, and_6_out, and_7_out, and_8_out, and_9_out, and_10_out,
       and_11_out, and_12_out, and_14_out, not_1_out;

  not not_1 (not_1_out, 1'b1);
  and and_1 (and_1_out, In[0], 1'b1);
  and and_2 (Out[0], not_1_out, In[1]);
  and and_3 (and_3_out, In[1], 1'b1);
  or or_1 (Out[1], and_1_out, and_4_out);
  and and_4 (and_4_out, not_1_out, In[2]);
  or or_2 (Out[2], and_3_out, and_6_out);
  and and_5 (and_5_out, In[2], 1'b1);
  and and_6 (and_6_out, not_1_out, In[3]);
  and and_7 (and_7_out, In[3], 1'b1);
  or or_3 (Out[3], and_5_out, and_8_out);
  and and_8 (and_8_out, not_1_out, In[4]);
  and and_9 (and_9_out, In[4], 1'b1);
  or or_4 (Out[4], and_7_out, and_11_out);
  and and_10 (and_10_out, In[5], 1'b1);
  and and_11 (and_11_out, not_1_out, In[5]);
  or or_5 (Out[5], and_9_out, and_12_out);
  and and_12 (and_12_out, not_1_out, In[6]);
  and and_13 (Out[7], In[6], 1'b1);
  or or_6 (Out[6], and_10_out, and_14_out);
  and and_14 (and_14_out, not_1_out, In[7]);

  assign Ovfl = In[7];
endmodule

module Filtro (
  input  [7:0] In,
  input  Crtl,
  output [7:0] Out
);

  and and_1 (Out[0], In[0], Crtl);
  and and_2 (Out[1], In[1], Crtl);
  and and_3 (Out[2], In[2], Crtl);
  and and_4 (Out[3], In[3], Crtl);
  and and_5 (Out[4], In[4], Crtl);
  and and_6 (Out[5], In[5], Crtl);
  and and_7 (Out[6], In[6], Crtl);
  and and_8 (Out[7], In[7], Crtl);
endmodule

module SignChange (
  input  [7:0] Num,
  output [7:0] out
);

  wire [7:0] inversor_1_out_2;

  Inversor inversor_1 (.in_1(Num), .out_2(inversor_1_out_2));
  Soma8bits soma8bits_1 (.Num1(8'h1), .Num2(inversor_1_out_2), .Result(out));  // open: Overflow
endmodule

module InversorCond (
  input  Ctrl,
  input  [7:0] Num,
  output [7:0] Out
);

  wire and_1_out, and_2_out, and_3_out, and_4_out, and_5_out, and_6_out, and_7_out, and_8_out, and_9_out,
       and_10_out, and_11_out, and_12_out, and_13_out, and_14_out, and_15_out, and_16_out, not_1_out,
       not_2_out, not_3_out, not_4_out, not_5_out, not_6_out, not_7_out, not_8_out, not_9_out;
  wire [7:0] signchange_1_out;

  SignChange signchange_1 (.Num(Num), .out(signchange_1_out));
  not not_1 (not_1_out, Ctrl);
  and and_1 (and_1_out, Num[0], not_1_out);
  and and_2 (and_2_out, Num[1], not_1_out);
  and and_3 (and_3_out, Num[2], not_1_out);
  and and_4 (and_4_out, Num[3], not_1_out);
  and and_5 (and_5_out, Num[4], not_1_out);
  and and_6 (and_6_out, Num[5], not_1_out);
  and and_7 (and_7_out, Num[6], not_1_out);
  and and_8 (and_8_out, Num[7], not_1_out);
  and and_9 (and_9_out, signchange_1_out[0], not_2_out);
  not not_2 (not_2_out, not_1_out);
  and and_10 (and_10_out, signchange_1_out[1], not_3_out);
  not not_3 (not_3_out, not_1_out);
  and and_11 (and_11_out, signchange_1_out[2], not_4_out);
  not not_4 (not_4_out, not_1_out);
  and and_12 (and_12_out, signchange_1_out[3], not_5_out);
  not not_5 (not_5_out, not_1_out);
  and and_13 (and_13_out, signchange_1_out[4], not_6_out);
  not not_6 (not_6_out, not_1_out);
  and and_14 (and_14_out, signchange_1_out[5], not_7_out);
  not not_7 (not_7_out, not_1_out);
  and and_15 (and_15_out, signchange_1_out[6], not_8_out);
  not not_8 (not_8_out, not_1_out);
  and and_16 (and_16_out, signchange_1_out[7], not_9_out);
  not not_9 (not_9_out, not_1_out);
  or or_1 (Out[0], and_1_out, and_9_out);
  or or_2 (Out[1], and_2_out, and_10_out);
  or or_3 (Out[2], and_3_out, and_11_out);
  or or_4 (Out[3], and_4_out, and_12_out);
  or or_5 (Out[4], and_5_out, and_13_out);
  or or_6 (Out[5], and_6_out, and_14_out);
  or or_7 (Out[6], and_7_out, and_15_out);
  or or_8 (Out[7], and_8_out, and_16_out);
endmodule
